// Logisim project processador_32bits.circ as structural Verilog: 9 circuits, main circuit celula operacoes
module via_de_dados (
  input  reset_banco,
  input  RESET,
  output [3:0] seletor_de_operacoes,
  output write,
  output [4:0] \endereço_write ,
  output [4:0] op_reg_A,
  output overflow,
  output [4:0] op_reg_B,
  output [31:0] ULA_data_B,
  output out_10
);

  wire and_2_out, and_3_out, clock_1_out, ULA_sao_iguais;
  wire [31:0] banco_registrador_1_datareg_a, banco_registrador_1_datareg_b, multiplexer_1_out,
       pc_mem_1_memout, ULA_saida;

  not not_1 (write, clock_1_out);
  Clock clock_1 (.out(clock_1_out));
  PC_MEM pc_mem_1 (
    .RESET(RESET), .MEMout(pc_mem_1_memout), .PC_CLK(clock_1_out),
    .estado_do_salto({ULA_data_B[31], ULA_data_B[16:8]}), .saltar(and_3_out));
  Register #(.width(32)) IR (
    .D(pc_mem_1_memout),
    .Q({ULA_data_B[31], ULA_data_B[16:5], op_reg_B, op_reg_A, \endereço_write , seletor_de_operacoes}),
    .clk(clock_1_out));  // open: en, clr
  banco_registrador banco_registrador_1 (
    .DATA_IN(ULA_saida), .registrador_A(op_reg_A), .write(write), .\endereço_write (\endereço_write ),
    .registrador_B(op_reg_B), .DATAreg_A(banco_registrador_1_datareg_a),
    .DATAreg_B(banco_registrador_1_datareg_b), .clear(reset_banco));
  Multiplexer #(.width(32), .enable("false")) multiplexer_1 (
    .in0(banco_registrador_1_datareg_b), .in1({{15{ULA_data_B[31]}}, ULA_data_B[16:5], op_reg_B}),
    .out(multiplexer_1_out), .sel(out_10));
  and and_1 (out_10, ~seletor_de_operacoes[0], ~seletor_de_operacoes[1], seletor_de_operacoes[2], ~seletor_de_operacoes[3]);  // AND_Gate
  ULA ULA (
    .B(multiplexer_1_out), .saida(ULA_saida), .operador(seletor_de_operacoes), .overflow(overflow),
    .sao_iguais(ULA_sao_iguais), .A(banco_registrador_1_datareg_a));
  and and_2 (and_2_out, ~seletor_de_operacoes[0], ~seletor_de_operacoes[1], ~seletor_de_operacoes[2], ~seletor_de_operacoes[3]);  // AND_Gate
  and and_3 (and_3_out, ULA_sao_iguais, and_2_out);

  assign {ULA_data_B[30:17], ULA_data_B[4:0]} = {{14{ULA_data_B[31]}}, op_reg_B};

  // Notes on the sheet:
  //   Banco
  //   endereco write
  //   op reg A
  //   op reg B
  //   ||
  //   _______________________________
  //   _______________________________
  //   E
  //   <--Seleciona endereço da memoria ram
  //   D
  //   ||
  //   ||
  //   ||
  //   ||
  //   C
  //   B
  //   ||
  //   A
  //   0 = and
  //   1 = or
  //   2 = xor
  //   3 = nand
  //   6 = subtrair
  //   7 = xnor
  //   Sistemas Digitais
  //   Aluno: Renato F. Soares
  //   TADS 2014.1
  //   4 = somar com valor externo
  //   5 = soma comp_2
  //   8 = desloca
  //   9 = compara A < B
  //   10 = somar com valor interno
  //   A: operador ula
  //   E: insere valor externo
  //   B: endereço da memoria para gravação no banco
  //   C: seleciona um valor do banco para o registrador A
  //   D: seleciona um valor do banco para o registrador B
endmodule

module celula_operacoes (
  input  transporte_entrada_____C_IN,
  input  transporte_entrada_____B_IN,
  input  entrada_desloca,
  input  [3:0] operador_MUX,
  input  A,
  input  B,
  input  b_in,
  input  C_in___compara,
  output C_out___compara,
  output saida,
  output transporte_saida_____C_OUT,
  output transporte_saida_____B_OUT,
  output saida_desloca,
  output [3:0] \Saída_operador 
);

  wire adder_1_out, adder_2_out, and_1_out, comparador_novo_1_a___b, nand_1_out, or_1_out, subtractor_1_out,
       xnor_1_out, xor_1_out;

  xnor xnor_1 (xnor_1_out, A, B);
  and and_1 (and_1_out, A, B);
  or or_1 (or_1_out, A, B);
  xor xor_1 (xor_1_out, A, B);
  nand nand_1 (nand_1_out, A, B);
  Adder #(.width(1)) adder_1 (
    .a(A), .b(B), .out(adder_1_out), .cin(transporte_entrada_____C_IN), .cout(transporte_saida_____C_OUT));
  comparador_novo comparador_novo_1 (
    .C_in(C_in___compara), .B(B), .A(A), .C_out(C_out___compara), .A___B(comparador_novo_1_a___b));
  Subtractor #(.width(1)) subtractor_1 (
    .a(A), .b(B), .out(subtractor_1_out), .bin(transporte_entrada_____B_IN), .bout(transporte_saida_____B_OUT));
  Multiplexer #(.select(4), .enable("false")) multiplexer_1 (
    .in0(and_1_out), .in1(or_1_out), .in2(xor_1_out), .in3(nand_1_out), .in4(adder_1_out), .in5(adder_1_out),
    .in6(subtractor_1_out), .in7(xnor_1_out), .in8(adder_2_out), .in9(comparador_novo_1_a___b),
    .in10(adder_1_out), .out(saida), .sel(operador_MUX));  // open: in11, in12, in13, in14, in15
  Adder #(.width(1)) adder_2 (.a(B), .b(b_in), .out(adder_2_out), .cin(entrada_desloca), .cout(saida_desloca));

  assign \Saída_operador  = operador_MUX;

  // Notes on the sheet:
  //   TADS 2014.1
  //   Celula de operações
  //   Sistemas Digitais
  //   Aluno: Renato Soares
  //   comparador
endmodule

module ULA (
  input  [3:0] operador,
  input  [31:0] A,
  input  [31:0] B,
  output overflow,
  output sao_iguais,
  output [31:0] saida
);

  wire and_1_out, celula_operacoes_1_saida_desloca, celula_operacoes_1_transporte_saida_____b_out,
       celula_operacoes_1_transporte_saida_____c_out, celula_operacoes_2_c_out___compara,
       celula_operacoes_2_saida_desloca, celula_operacoes_2_transporte_saida_____b_out,
       celula_operacoes_2_transporte_saida_____c_out, celula_operacoes_3_c_out___compara,
       celula_operacoes_3_saida_desloca, celula_operacoes_3_transporte_saida_____b_out,
       celula_operacoes_3_transporte_saida_____c_out, celula_operacoes_4_c_out___compara,
       celula_operacoes_4_saida_desloca, celula_operacoes_4_transporte_saida_____b_out,
       celula_operacoes_4_transporte_saida_____c_out, celula_operacoes_5_c_out___compara,
       celula_operacoes_5_saida_desloca, celula_operacoes_5_transporte_saida_____b_out,
       celula_operacoes_5_transporte_saida_____c_out, celula_operacoes_6_c_out___compara,
       celula_operacoes_6_saida_desloca, celula_operacoes_6_transporte_saida_____b_out,
       celula_operacoes_6_transporte_saida_____c_out, celula_operacoes_7_c_out___compara,
       celula_operacoes_7_saida_desloca, celula_operacoes_7_transporte_saida_____b_out,
       celula_operacoes_7_transporte_saida_____c_out, celula_operacoes_8_c_out___compara,
       celula_operacoes_8_saida_desloca, celula_operacoes_8_transporte_saida_____b_out,
       celula_operacoes_8_transporte_saida_____c_out, celula_operacoes_9_c_out___compara,
       celula_operacoes_9_saida_desloca, celula_operacoes_9_transporte_saida_____b_out,
       celula_operacoes_9_transporte_saida_____c_out, celula_operacoes_10_c_out___compara,
       celula_operacoes_10_saida_desloca, celula_operacoes_10_transporte_saida_____b_out,
       celula_operacoes_10_transporte_saida_____c_out, celula_operacoes_11_c_out___compara,
       celula_operacoes_11_saida_desloca, celula_operacoes_11_transporte_saida_____b_out,
       celula_operacoes_11_transporte_saida_____c_out, celula_operacoes_12_c_out___compara,
       celula_operacoes_12_saida_desloca, celula_operacoes_12_transporte_saida_____b_out,
       celula_operacoes_12_transporte_saida_____c_out, celula_operacoes_13_c_out___compara,
       celula_operacoes_13_saida_desloca, celula_operacoes_13_transporte_saida_____b_out,
       celula_operacoes_13_transporte_saida_____c_out, celula_operacoes_14_c_out___compara,
       celula_operacoes_14_saida_desloca, celula_operacoes_14_transporte_saida_____b_out,
       celula_operacoes_14_transporte_saida_____c_out, celula_operacoes_15_c_out___compara,
       celula_operacoes_15_saida_desloca, celula_operacoes_15_transporte_saida_____b_out,
       celula_operacoes_15_transporte_saida_____c_out, celula_operacoes_16_c_out___compara,
       celula_operacoes_16_saida_desloca, celula_operacoes_16_transporte_saida_____b_out,
       celula_operacoes_16_transporte_saida_____c_out, celula_operacoes_17_c_out___compara,
       celula_operacoes_17_saida_desloca, celula_operacoes_17_transporte_saida_____b_out,
       celula_operacoes_17_transporte_saida_____c_out, celula_operacoes_18_c_out___compara,
       celula_operacoes_18_saida_desloca, celula_operacoes_18_transporte_saida_____b_out,
       celula_operacoes_18_transporte_saida_____c_out, celula_operacoes_19_c_out___compara,
       celula_operacoes_19_saida_desloca, celula_operacoes_19_transporte_saida_____b_out,
       celula_operacoes_19_transporte_saida_____c_out, celula_operacoes_20_c_out___compara,
       celula_operacoes_20_saida_desloca, celula_operacoes_20_transporte_saida_____b_out,
       celula_operacoes_20_transporte_saida_____c_out, celula_operacoes_21_c_out___compara,
       celula_operacoes_21_saida_desloca, celula_operacoes_21_transporte_saida_____b_out,
       celula_operacoes_21_transporte_saida_____c_out, celula_operacoes_22_c_out___compara,
       celula_operacoes_22_saida_desloca, celula_operacoes_22_transporte_saida_____b_out,
       celula_operacoes_22_transporte_saida_____c_out, celula_operacoes_23_c_out___compara,
       celula_operacoes_23_saida_desloca, celula_operacoes_23_transporte_saida_____b_out,
       celula_operacoes_23_transporte_saida_____c_out, celula_operacoes_24_c_out___compara,
       celula_operacoes_24_saida_desloca, celula_operacoes_24_transporte_saida_____b_out,
       celula_operacoes_24_transporte_saida_____c_out, celula_operacoes_25_c_out___compara,
       celula_operacoes_25_saida_desloca, celula_operacoes_25_transporte_saida_____b_out,
       celula_operacoes_25_transporte_saida_____c_out, celula_operacoes_26_c_out___compara,
       celula_operacoes_26_saida_desloca, celula_operacoes_26_transporte_saida_____b_out,
       celula_operacoes_26_transporte_saida_____c_out, celula_operacoes_27_c_out___compara,
       celula_operacoes_27_saida_desloca, celula_operacoes_27_transporte_saida_____b_out,
       celula_operacoes_27_transporte_saida_____c_out, celula_operacoes_28_c_out___compara,
       celula_operacoes_28_saida_desloca, celula_operacoes_28_transporte_saida_____b_out,
       celula_operacoes_28_transporte_saida_____c_out, celula_operacoes_29_c_out___compara,
       celula_operacoes_29_saida_desloca, celula_operacoes_29_transporte_saida_____b_out,
       celula_operacoes_29_transporte_saida_____c_out, celula_operacoes_30_c_out___compara,
       celula_operacoes_30_saida_desloca, celula_operacoes_30_transporte_saida_____b_out,
       celula_operacoes_30_transporte_saida_____c_out, celula_operacoes_31_c_out___compara,
       celula_operacoes_31_saida_desloca, celula_operacoes_31_transporte_saida_____b_out,
       celula_operacoes_31_transporte_saida_____c_out, celula_operacoes_32_c_out___compara,
       celula_operacoes_32_saida_desloca, celula_operacoes_32_transporte_saida_____b_out,
       celula_operacoes_32_transporte_saida_____c_out, xnor_1_out, xor_1_out;
  wire [3:0] \celula_operacoes_1_saída_operador , \celula_operacoes_2_saída_operador ,
       \celula_operacoes_3_saída_operador , \celula_operacoes_4_saída_operador ,
       \celula_operacoes_5_saída_operador , \celula_operacoes_6_saída_operador ,
       \celula_operacoes_7_saída_operador , \celula_operacoes_8_saída_operador ,
       \celula_operacoes_9_saída_operador , \celula_operacoes_10_saída_operador ,
       \celula_operacoes_11_saída_operador , \celula_operacoes_12_saída_operador ,
       \celula_operacoes_13_saída_operador , \celula_operacoes_14_saída_operador ,
       \celula_operacoes_15_saída_operador , \celula_operacoes_16_saída_operador ,
       \celula_operacoes_18_saída_operador , \celula_operacoes_19_saída_operador ,
       \celula_operacoes_20_saída_operador , \celula_operacoes_21_saída_operador ,
       \celula_operacoes_22_saída_operador , \celula_operacoes_23_saída_operador ,
       \celula_operacoes_24_saída_operador , \celula_operacoes_25_saída_operador ,
       \celula_operacoes_26_saída_operador , \celula_operacoes_27_saída_operador ,
       \celula_operacoes_28_saída_operador , \celula_operacoes_29_saída_operador ,
       \celula_operacoes_30_saída_operador , \celula_operacoes_31_saída_operador ,
       \celula_operacoes_32_saída_operador ;

  celula_operacoes celula_operacoes_1 (
    .A(A[0]), .B(B[0]), .b_in(B[0]), .saida(saida[0]), .entrada_desloca(1'b0),
    .transporte_entrada_____C_IN(1'b0), .transporte_entrada_____B_IN(1'b0), .operador_MUX(operador),
    .transporte_saida_____C_OUT(celula_operacoes_1_transporte_saida_____c_out),
    .saida_desloca(celula_operacoes_1_saida_desloca),
    .transporte_saida_____B_OUT(celula_operacoes_1_transporte_saida_____b_out),
    .\Saída_operador (\celula_operacoes_1_saída_operador ),
    .C_in___compara(celula_operacoes_2_c_out___compara));  // open: C_out___compara
  celula_operacoes celula_operacoes_2 (
    .A(A[1]), .B(B[1]), .b_in(B[1]), .saida(saida[1]), .entrada_desloca(celula_operacoes_1_saida_desloca),
    .transporte_entrada_____C_IN(celula_operacoes_1_transporte_saida_____c_out),
    .transporte_entrada_____B_IN(celula_operacoes_1_transporte_saida_____b_out),
    .operador_MUX(\celula_operacoes_1_saída_operador ),
    .transporte_saida_____C_OUT(celula_operacoes_2_transporte_saida_____c_out),
    .saida_desloca(celula_operacoes_2_saida_desloca),
    .transporte_saida_____B_OUT(celula_operacoes_2_transporte_saida_____b_out),
    .\Saída_operador (\celula_operacoes_2_saída_operador ),
    .C_in___compara(celula_operacoes_3_c_out___compara), .C_out___compara(celula_operacoes_2_c_out___compara));
  celula_operacoes celula_operacoes_3 (
    .A(A[2]), .B(B[2]), .b_in(B[2]), .saida(saida[2]), .entrada_desloca(celula_operacoes_2_saida_desloca),
    .transporte_entrada_____C_IN(celula_operacoes_2_transporte_saida_____c_out),
    .transporte_entrada_____B_IN(celula_operacoes_2_transporte_saida_____b_out),
    .operador_MUX(\celula_operacoes_2_saída_operador ),
    .transporte_saida_____C_OUT(celula_operacoes_3_transporte_saida_____c_out),
    .saida_desloca(celula_operacoes_3_saida_desloca),
    .transporte_saida_____B_OUT(celula_operacoes_3_transporte_saida_____b_out),
    .\Saída_operador (\celula_operacoes_3_saída_operador ),
    .C_in___compara(celula_operacoes_4_c_out___compara), .C_out___compara(celula_operacoes_3_c_out___compara));
  celula_operacoes celula_operacoes_4 (
    .A(A[3]), .B(B[3]), .b_in(B[3]), .saida(saida[3]), .entrada_desloca(celula_operacoes_3_saida_desloca),
    .transporte_entrada_____C_IN(celula_operacoes_3_transporte_saida_____c_out),
    .transporte_entrada_____B_IN(celula_operacoes_3_transporte_saida_____b_out),
    .operador_MUX(\celula_operacoes_3_saída_operador ),
    .transporte_saida_____C_OUT(celula_operacoes_4_transporte_saida_____c_out),
    .saida_desloca(celula_operacoes_4_saida_desloca),
    .transporte_saida_____B_OUT(celula_operacoes_4_transporte_saida_____b_out),
    .\Saída_operador (\celula_operacoes_4_saída_operador ),
    .C_in___compara(celula_operacoes_5_c_out___compara), .C_out___compara(celula_operacoes_4_c_out___compara));
  celula_operacoes celula_operacoes_5 (
    .A(A[4]), .B(B[4]), .b_in(B[4]), .saida(saida[4]), .entrada_desloca(celula_operacoes_4_saida_desloca),
    .transporte_entrada_____C_IN(celula_operacoes_4_transporte_saida_____c_out),
    .transporte_entrada_____B_IN(celula_operacoes_4_transporte_saida_____b_out),
    .operador_MUX(\celula_operacoes_4_saída_operador ),
    .transporte_saida_____C_OUT(celula_operacoes_5_transporte_saida_____c_out),
    .saida_desloca(celula_operacoes_5_saida_desloca),
    .transporte_saida_____B_OUT(celula_operacoes_5_transporte_saida_____b_out),
    .\Saída_operador (\celula_operacoes_5_saída_operador ),
    .C_in___compara(celula_operacoes_6_c_out___compara), .C_out___compara(celula_operacoes_5_c_out___compara));
  celula_operacoes celula_operacoes_6 (
    .A(A[5]), .B(B[5]), .b_in(B[5]), .saida(saida[5]), .entrada_desloca(celula_operacoes_5_saida_desloca),
    .transporte_entrada_____C_IN(celula_operacoes_5_transporte_saida_____c_out),
    .transporte_entrada_____B_IN(celula_operacoes_5_transporte_saida_____b_out),
    .operador_MUX(\celula_operacoes_5_saída_operador ),
    .transporte_saida_____C_OUT(celula_operacoes_6_transporte_saida_____c_out),
    .saida_desloca(celula_operacoes_6_saida_desloca),
    .transporte_saida_____B_OUT(celula_operacoes_6_transporte_saida_____b_out),
    .\Saída_operador (\celula_operacoes_6_saída_operador ),
    .C_in___compara(celula_operacoes_7_c_out___compara), .C_out___compara(celula_operacoes_6_c_out___compara));
  celula_operacoes celula_operacoes_7 (
    .A(A[6]), .B(B[6]), .b_in(B[6]), .saida(saida[6]), .entrada_desloca(celula_operacoes_6_saida_desloca),
    .transporte_entrada_____C_IN(celula_operacoes_6_transporte_saida_____c_out),
    .transporte_entrada_____B_IN(celula_operacoes_6_transporte_saida_____b_out),
    .operador_MUX(\celula_operacoes_6_saída_operador ),
    .transporte_saida_____C_OUT(celula_operacoes_7_transporte_saida_____c_out),
    .saida_desloca(celula_operacoes_7_saida_desloca),
    .transporte_saida_____B_OUT(celula_operacoes_7_transporte_saida_____b_out),
    .\Saída_operador (\celula_operacoes_7_saída_operador ),
    .C_in___compara(celula_operacoes_8_c_out___compara), .C_out___compara(celula_operacoes_7_c_out___compara));
  celula_operacoes celula_operacoes_8 (
    .A(A[7]), .B(B[7]), .b_in(B[7]), .saida(saida[7]), .entrada_desloca(celula_operacoes_7_saida_desloca),
    .transporte_entrada_____C_IN(celula_operacoes_7_transporte_saida_____c_out),
    .transporte_entrada_____B_IN(celula_operacoes_7_transporte_saida_____b_out),
    .operador_MUX(\celula_operacoes_7_saída_operador ),
    .transporte_saida_____C_OUT(celula_operacoes_8_transporte_saida_____c_out),
    .saida_desloca(celula_operacoes_8_saida_desloca),
    .transporte_saida_____B_OUT(celula_operacoes_8_transporte_saida_____b_out),
    .\Saída_operador (\celula_operacoes_8_saída_operador ),
    .C_in___compara(celula_operacoes_9_c_out___compara), .C_out___compara(celula_operacoes_8_c_out___compara));
  celula_operacoes celula_operacoes_9 (
    .A(A[8]), .B(B[8]), .b_in(B[8]), .saida(saida[8]), .entrada_desloca(celula_operacoes_8_saida_desloca),
    .transporte_entrada_____C_IN(celula_operacoes_8_transporte_saida_____c_out),
    .transporte_entrada_____B_IN(celula_operacoes_8_transporte_saida_____b_out),
    .operador_MUX(\celula_operacoes_8_saída_operador ),
    .transporte_saida_____C_OUT(celula_operacoes_9_transporte_saida_____c_out),
    .saida_desloca(celula_operacoes_9_saida_desloca),
    .transporte_saida_____B_OUT(celula_operacoes_9_transporte_saida_____b_out),
    .\Saída_operador (\celula_operacoes_9_saída_operador ),
    .C_in___compara(celula_operacoes_10_c_out___compara), .C_out___compara(celula_operacoes_9_c_out___compara));
  celula_operacoes celula_operacoes_10 (
    .A(A[9]), .B(B[9]), .b_in(B[9]), .saida(saida[9]), .entrada_desloca(celula_operacoes_9_saida_desloca),
    .transporte_entrada_____C_IN(celula_operacoes_9_transporte_saida_____c_out),
    .transporte_entrada_____B_IN(celula_operacoes_9_transporte_saida_____b_out),
    .operador_MUX(\celula_operacoes_9_saída_operador ),
    .transporte_saida_____C_OUT(celula_operacoes_10_transporte_saida_____c_out),
    .saida_desloca(celula_operacoes_10_saida_desloca),
    .transporte_saida_____B_OUT(celula_operacoes_10_transporte_saida_____b_out),
    .\Saída_operador (\celula_operacoes_10_saída_operador ),
    .C_in___compara(celula_operacoes_11_c_out___compara),
    .C_out___compara(celula_operacoes_10_c_out___compara));
  celula_operacoes celula_operacoes_11 (
    .A(A[10]), .B(B[10]), .b_in(B[10]), .saida(saida[10]),
    .entrada_desloca(celula_operacoes_10_saida_desloca),
    .transporte_entrada_____C_IN(celula_operacoes_10_transporte_saida_____c_out),
    .transporte_entrada_____B_IN(celula_operacoes_10_transporte_saida_____b_out),
    .operador_MUX(\celula_operacoes_10_saída_operador ),
    .transporte_saida_____C_OUT(celula_operacoes_11_transporte_saida_____c_out),
    .saida_desloca(celula_operacoes_11_saida_desloca),
    .transporte_saida_____B_OUT(celula_operacoes_11_transporte_saida_____b_out),
    .\Saída_operador (\celula_operacoes_11_saída_operador ),
    .C_in___compara(celula_operacoes_12_c_out___compara),
    .C_out___compara(celula_operacoes_11_c_out___compara));
  celula_operacoes celula_operacoes_12 (
    .A(A[11]), .B(B[11]), .b_in(B[11]), .saida(saida[11]),
    .entrada_desloca(celula_operacoes_11_saida_desloca),
    .transporte_entrada_____C_IN(celula_operacoes_11_transporte_saida_____c_out),
    .transporte_entrada_____B_IN(celula_operacoes_11_transporte_saida_____b_out),
    .operador_MUX(\celula_operacoes_11_saída_operador ),
    .transporte_saida_____C_OUT(celula_operacoes_12_transporte_saida_____c_out),
    .saida_desloca(celula_operacoes_12_saida_desloca),
    .transporte_saida_____B_OUT(celula_operacoes_12_transporte_saida_____b_out),
    .\Saída_operador (\celula_operacoes_12_saída_operador ),
    .C_in___compara(celula_operacoes_13_c_out___compara),
    .C_out___compara(celula_operacoes_12_c_out___compara));
  celula_operacoes celula_operacoes_13 (
    .A(A[12]), .B(B[12]), .b_in(B[12]), .saida(saida[12]),
    .entrada_desloca(celula_operacoes_12_saida_desloca),
    .transporte_entrada_____C_IN(celula_operacoes_12_transporte_saida_____c_out),
    .transporte_entrada_____B_IN(celula_operacoes_12_transporte_saida_____b_out),
    .operador_MUX(\celula_operacoes_12_saída_operador ),
    .transporte_saida_____C_OUT(celula_operacoes_13_transporte_saida_____c_out),
    .saida_desloca(celula_operacoes_13_saida_desloca),
    .transporte_saida_____B_OUT(celula_operacoes_13_transporte_saida_____b_out),
    .\Saída_operador (\celula_operacoes_13_saída_operador ),
    .C_in___compara(celula_operacoes_14_c_out___compara),
    .C_out___compara(celula_operacoes_13_c_out___compara));
  celula_operacoes celula_operacoes_14 (
    .A(A[13]), .B(B[13]), .b_in(B[13]), .saida(saida[13]),
    .entrada_desloca(celula_operacoes_13_saida_desloca),
    .transporte_entrada_____C_IN(celula_operacoes_13_transporte_saida_____c_out),
    .transporte_entrada_____B_IN(celula_operacoes_13_transporte_saida_____b_out),
    .operador_MUX(\celula_operacoes_13_saída_operador ),
    .transporte_saida_____C_OUT(celula_operacoes_14_transporte_saida_____c_out),
    .saida_desloca(celula_operacoes_14_saida_desloca),
    .transporte_saida_____B_OUT(celula_operacoes_14_transporte_saida_____b_out),
    .\Saída_operador (\celula_operacoes_14_saída_operador ),
    .C_in___compara(celula_operacoes_15_c_out___compara),
    .C_out___compara(celula_operacoes_14_c_out___compara));
  celula_operacoes celula_operacoes_15 (
    .A(A[14]), .B(B[14]), .b_in(B[14]), .saida(saida[14]),
    .entrada_desloca(celula_operacoes_14_saida_desloca),
    .transporte_entrada_____C_IN(celula_operacoes_14_transporte_saida_____c_out),
    .transporte_entrada_____B_IN(celula_operacoes_14_transporte_saida_____b_out),
    .operador_MUX(\celula_operacoes_14_saída_operador ),
    .transporte_saida_____C_OUT(celula_operacoes_15_transporte_saida_____c_out),
    .saida_desloca(celula_operacoes_15_saida_desloca),
    .transporte_saida_____B_OUT(celula_operacoes_15_transporte_saida_____b_out),
    .\Saída_operador (\celula_operacoes_15_saída_operador ),
    .C_in___compara(celula_operacoes_16_c_out___compara),
    .C_out___compara(celula_operacoes_15_c_out___compara));
  celula_operacoes celula_operacoes_16 (
    .A(A[15]), .B(B[15]), .b_in(B[15]), .saida(saida[15]),
    .entrada_desloca(celula_operacoes_15_saida_desloca),
    .transporte_entrada_____C_IN(celula_operacoes_15_transporte_saida_____c_out),
    .transporte_entrada_____B_IN(celula_operacoes_15_transporte_saida_____b_out),
    .operador_MUX(\celula_operacoes_15_saída_operador ),
    .transporte_saida_____C_OUT(celula_operacoes_16_transporte_saida_____c_out),
    .saida_desloca(celula_operacoes_16_saida_desloca),
    .transporte_saida_____B_OUT(celula_operacoes_16_transporte_saida_____b_out),
    .\Saída_operador (\celula_operacoes_16_saída_operador ),
    .C_in___compara(celula_operacoes_32_c_out___compara),
    .C_out___compara(celula_operacoes_16_c_out___compara));
  celula_operacoes celula_operacoes_17 (
    .A(A[31]), .B(B[31]), .b_in(B[31]), .saida(saida[31]),
    .entrada_desloca(celula_operacoes_18_saida_desloca),
    .transporte_entrada_____C_IN(celula_operacoes_18_transporte_saida_____c_out),
    .transporte_entrada_____B_IN(celula_operacoes_18_transporte_saida_____b_out),
    .operador_MUX(\celula_operacoes_18_saída_operador ),
    .transporte_saida_____C_OUT(celula_operacoes_17_transporte_saida_____c_out),
    .saida_desloca(celula_operacoes_17_saida_desloca),
    .transporte_saida_____B_OUT(celula_operacoes_17_transporte_saida_____b_out), .C_in___compara(1'b1),
    .C_out___compara(celula_operacoes_17_c_out___compara));  // open: Saída_operador
  celula_operacoes celula_operacoes_18 (
    .A(A[30]), .B(B[30]), .b_in(B[30]), .saida(saida[30]),
    .entrada_desloca(celula_operacoes_19_saida_desloca),
    .transporte_entrada_____C_IN(celula_operacoes_19_transporte_saida_____c_out),
    .transporte_entrada_____B_IN(celula_operacoes_19_transporte_saida_____b_out),
    .operador_MUX(\celula_operacoes_19_saída_operador ),
    .transporte_saida_____C_OUT(celula_operacoes_18_transporte_saida_____c_out),
    .saida_desloca(celula_operacoes_18_saida_desloca),
    .transporte_saida_____B_OUT(celula_operacoes_18_transporte_saida_____b_out),
    .\Saída_operador (\celula_operacoes_18_saída_operador ),
    .C_in___compara(celula_operacoes_17_c_out___compara),
    .C_out___compara(celula_operacoes_18_c_out___compara));
  celula_operacoes celula_operacoes_19 (
    .A(A[29]), .B(B[29]), .b_in(B[29]), .saida(saida[29]),
    .entrada_desloca(celula_operacoes_20_saida_desloca),
    .transporte_entrada_____C_IN(celula_operacoes_20_transporte_saida_____c_out),
    .transporte_entrada_____B_IN(celula_operacoes_20_transporte_saida_____b_out),
    .operador_MUX(\celula_operacoes_20_saída_operador ),
    .transporte_saida_____C_OUT(celula_operacoes_19_transporte_saida_____c_out),
    .saida_desloca(celula_operacoes_19_saida_desloca),
    .transporte_saida_____B_OUT(celula_operacoes_19_transporte_saida_____b_out),
    .\Saída_operador (\celula_operacoes_19_saída_operador ),
    .C_in___compara(celula_operacoes_18_c_out___compara),
    .C_out___compara(celula_operacoes_19_c_out___compara));
  celula_operacoes celula_operacoes_20 (
    .A(A[28]), .B(B[28]), .b_in(B[28]), .saida(saida[28]),
    .entrada_desloca(celula_operacoes_21_saida_desloca),
    .transporte_entrada_____C_IN(celula_operacoes_21_transporte_saida_____c_out),
    .transporte_entrada_____B_IN(celula_operacoes_21_transporte_saida_____b_out),
    .operador_MUX(\celula_operacoes_21_saída_operador ),
    .transporte_saida_____C_OUT(celula_operacoes_20_transporte_saida_____c_out),
    .saida_desloca(celula_operacoes_20_saida_desloca),
    .transporte_saida_____B_OUT(celula_operacoes_20_transporte_saida_____b_out),
    .\Saída_operador (\celula_operacoes_20_saída_operador ),
    .C_in___compara(celula_operacoes_19_c_out___compara),
    .C_out___compara(celula_operacoes_20_c_out___compara));
  celula_operacoes celula_operacoes_21 (
    .A(A[27]), .B(B[27]), .b_in(B[27]), .saida(saida[27]),
    .entrada_desloca(celula_operacoes_22_saida_desloca),
    .transporte_entrada_____C_IN(celula_operacoes_22_transporte_saida_____c_out),
    .transporte_entrada_____B_IN(celula_operacoes_22_transporte_saida_____b_out),
    .operador_MUX(\celula_operacoes_22_saída_operador ),
    .transporte_saida_____C_OUT(celula_operacoes_21_transporte_saida_____c_out),
    .saida_desloca(celula_operacoes_21_saida_desloca),
    .transporte_saida_____B_OUT(celula_operacoes_21_transporte_saida_____b_out),
    .\Saída_operador (\celula_operacoes_21_saída_operador ),
    .C_in___compara(celula_operacoes_20_c_out___compara),
    .C_out___compara(celula_operacoes_21_c_out___compara));
  celula_operacoes celula_operacoes_22 (
    .A(A[26]), .B(B[26]), .b_in(B[26]), .saida(saida[26]),
    .entrada_desloca(celula_operacoes_23_saida_desloca),
    .transporte_entrada_____C_IN(celula_operacoes_23_transporte_saida_____c_out),
    .transporte_entrada_____B_IN(celula_operacoes_23_transporte_saida_____b_out),
    .operador_MUX(\celula_operacoes_23_saída_operador ),
    .transporte_saida_____C_OUT(celula_operacoes_22_transporte_saida_____c_out),
    .saida_desloca(celula_operacoes_22_saida_desloca),
    .transporte_saida_____B_OUT(celula_operacoes_22_transporte_saida_____b_out),
    .\Saída_operador (\celula_operacoes_22_saída_operador ),
    .C_in___compara(celula_operacoes_21_c_out___compara),
    .C_out___compara(celula_operacoes_22_c_out___compara));
  celula_operacoes celula_operacoes_23 (
    .A(A[25]), .B(B[25]), .b_in(B[25]), .saida(saida[25]),
    .entrada_desloca(celula_operacoes_24_saida_desloca),
    .transporte_entrada_____C_IN(celula_operacoes_24_transporte_saida_____c_out),
    .transporte_entrada_____B_IN(celula_operacoes_24_transporte_saida_____b_out),
    .operador_MUX(\celula_operacoes_24_saída_operador ),
    .transporte_saida_____C_OUT(celula_operacoes_23_transporte_saida_____c_out),
    .saida_desloca(celula_operacoes_23_saida_desloca),
    .transporte_saida_____B_OUT(celula_operacoes_23_transporte_saida_____b_out),
    .\Saída_operador (\celula_operacoes_23_saída_operador ),
    .C_in___compara(celula_operacoes_22_c_out___compara),
    .C_out___compara(celula_operacoes_23_c_out___compara));
  celula_operacoes celula_operacoes_24 (
    .A(A[24]), .B(B[24]), .b_in(B[24]), .saida(saida[24]),
    .entrada_desloca(celula_operacoes_25_saida_desloca),
    .transporte_entrada_____C_IN(celula_operacoes_25_transporte_saida_____c_out),
    .transporte_entrada_____B_IN(celula_operacoes_25_transporte_saida_____b_out),
    .operador_MUX(\celula_operacoes_25_saída_operador ),
    .transporte_saida_____C_OUT(celula_operacoes_24_transporte_saida_____c_out),
    .saida_desloca(celula_operacoes_24_saida_desloca),
    .transporte_saida_____B_OUT(celula_operacoes_24_transporte_saida_____b_out),
    .\Saída_operador (\celula_operacoes_24_saída_operador ),
    .C_in___compara(celula_operacoes_23_c_out___compara),
    .C_out___compara(celula_operacoes_24_c_out___compara));
  celula_operacoes celula_operacoes_25 (
    .A(A[23]), .B(B[23]), .b_in(B[23]), .saida(saida[23]),
    .entrada_desloca(celula_operacoes_26_saida_desloca),
    .transporte_entrada_____C_IN(celula_operacoes_26_transporte_saida_____c_out),
    .transporte_entrada_____B_IN(celula_operacoes_26_transporte_saida_____b_out),
    .operador_MUX(\celula_operacoes_26_saída_operador ),
    .transporte_saida_____C_OUT(celula_operacoes_25_transporte_saida_____c_out),
    .saida_desloca(celula_operacoes_25_saida_desloca),
    .transporte_saida_____B_OUT(celula_operacoes_25_transporte_saida_____b_out),
    .\Saída_operador (\celula_operacoes_25_saída_operador ),
    .C_in___compara(celula_operacoes_24_c_out___compara),
    .C_out___compara(celula_operacoes_25_c_out___compara));
  celula_operacoes celula_operacoes_26 (
    .A(A[22]), .B(B[22]), .b_in(B[22]), .saida(saida[22]),
    .entrada_desloca(celula_operacoes_27_saida_desloca),
    .transporte_entrada_____C_IN(celula_operacoes_27_transporte_saida_____c_out),
    .transporte_entrada_____B_IN(celula_operacoes_27_transporte_saida_____b_out),
    .operador_MUX(\celula_operacoes_27_saída_operador ),
    .transporte_saida_____C_OUT(celula_operacoes_26_transporte_saida_____c_out),
    .saida_desloca(celula_operacoes_26_saida_desloca),
    .transporte_saida_____B_OUT(celula_operacoes_26_transporte_saida_____b_out),
    .\Saída_operador (\celula_operacoes_26_saída_operador ),
    .C_in___compara(celula_operacoes_25_c_out___compara),
    .C_out___compara(celula_operacoes_26_c_out___compara));
  celula_operacoes celula_operacoes_27 (
    .A(A[21]), .B(B[21]), .b_in(B[21]), .saida(saida[21]),
    .entrada_desloca(celula_operacoes_28_saida_desloca),
    .transporte_entrada_____C_IN(celula_operacoes_28_transporte_saida_____c_out),
    .transporte_entrada_____B_IN(celula_operacoes_28_transporte_saida_____b_out),
    .operador_MUX(\celula_operacoes_28_saída_operador ),
    .transporte_saida_____C_OUT(celula_operacoes_27_transporte_saida_____c_out),
    .saida_desloca(celula_operacoes_27_saida_desloca),
    .transporte_saida_____B_OUT(celula_operacoes_27_transporte_saida_____b_out),
    .\Saída_operador (\celula_operacoes_27_saída_operador ),
    .C_in___compara(celula_operacoes_26_c_out___compara),
    .C_out___compara(celula_operacoes_27_c_out___compara));
  celula_operacoes celula_operacoes_28 (
    .A(A[20]), .B(B[20]), .b_in(B[20]), .saida(saida[20]),
    .entrada_desloca(celula_operacoes_29_saida_desloca),
    .transporte_entrada_____C_IN(celula_operacoes_29_transporte_saida_____c_out),
    .transporte_entrada_____B_IN(celula_operacoes_29_transporte_saida_____b_out),
    .operador_MUX(\celula_operacoes_29_saída_operador ),
    .transporte_saida_____C_OUT(celula_operacoes_28_transporte_saida_____c_out),
    .saida_desloca(celula_operacoes_28_saida_desloca),
    .transporte_saida_____B_OUT(celula_operacoes_28_transporte_saida_____b_out),
    .\Saída_operador (\celula_operacoes_28_saída_operador ),
    .C_in___compara(celula_operacoes_27_c_out___compara),
    .C_out___compara(celula_operacoes_28_c_out___compara));
  celula_operacoes celula_operacoes_29 (
    .A(A[19]), .B(B[19]), .b_in(B[19]), .saida(saida[19]),
    .entrada_desloca(celula_operacoes_30_saida_desloca),
    .transporte_entrada_____C_IN(celula_operacoes_30_transporte_saida_____c_out),
    .transporte_entrada_____B_IN(celula_operacoes_30_transporte_saida_____b_out),
    .operador_MUX(\celula_operacoes_30_saída_operador ),
    .transporte_saida_____C_OUT(celula_operacoes_29_transporte_saida_____c_out),
    .saida_desloca(celula_operacoes_29_saida_desloca),
    .transporte_saida_____B_OUT(celula_operacoes_29_transporte_saida_____b_out),
    .\Saída_operador (\celula_operacoes_29_saída_operador ),
    .C_in___compara(celula_operacoes_28_c_out___compara),
    .C_out___compara(celula_operacoes_29_c_out___compara));
  celula_operacoes celula_operacoes_30 (
    .A(A[18]), .B(B[18]), .b_in(B[18]), .saida(saida[18]),
    .entrada_desloca(celula_operacoes_31_saida_desloca),
    .transporte_entrada_____C_IN(celula_operacoes_31_transporte_saida_____c_out),
    .transporte_entrada_____B_IN(celula_operacoes_31_transporte_saida_____b_out),
    .operador_MUX(\celula_operacoes_31_saída_operador ),
    .transporte_saida_____C_OUT(celula_operacoes_30_transporte_saida_____c_out),
    .saida_desloca(celula_operacoes_30_saida_desloca),
    .transporte_saida_____B_OUT(celula_operacoes_30_transporte_saida_____b_out),
    .\Saída_operador (\celula_operacoes_30_saída_operador ),
    .C_in___compara(celula_operacoes_29_c_out___compara),
    .C_out___compara(celula_operacoes_30_c_out___compara));
  celula_operacoes celula_operacoes_31 (
    .A(A[17]), .B(B[17]), .b_in(B[17]), .saida(saida[17]),
    .entrada_desloca(celula_operacoes_32_saida_desloca),
    .transporte_entrada_____C_IN(celula_operacoes_32_transporte_saida_____c_out),
    .transporte_entrada_____B_IN(celula_operacoes_32_transporte_saida_____b_out),
    .operador_MUX(\celula_operacoes_32_saída_operador ),
    .transporte_saida_____C_OUT(celula_operacoes_31_transporte_saida_____c_out),
    .saida_desloca(celula_operacoes_31_saida_desloca),
    .transporte_saida_____B_OUT(celula_operacoes_31_transporte_saida_____b_out),
    .\Saída_operador (\celula_operacoes_31_saída_operador ),
    .C_in___compara(celula_operacoes_30_c_out___compara),
    .C_out___compara(celula_operacoes_31_c_out___compara));
  celula_operacoes celula_operacoes_32 (
    .A(A[16]), .B(B[16]), .b_in(B[16]), .saida(saida[16]),
    .entrada_desloca(celula_operacoes_16_saida_desloca),
    .transporte_entrada_____C_IN(celula_operacoes_16_transporte_saida_____c_out),
    .transporte_entrada_____B_IN(celula_operacoes_16_transporte_saida_____b_out),
    .operador_MUX(\celula_operacoes_16_saída_operador ),
    .transporte_saida_____C_OUT(celula_operacoes_32_transporte_saida_____c_out),
    .saida_desloca(celula_operacoes_32_saida_desloca),
    .transporte_saida_____B_OUT(celula_operacoes_32_transporte_saida_____b_out),
    .\Saída_operador (\celula_operacoes_32_saída_operador ),
    .C_in___compara(celula_operacoes_31_c_out___compara),
    .C_out___compara(celula_operacoes_32_c_out___compara));
  xnor xnor_1 (xnor_1_out, A[31], B[31]);
  xor xor_1 (xor_1_out, B[31], saida[31]);
  and and_1 (and_1_out, xnor_1_out, xor_1_out);
  or or_1 (overflow, celula_operacoes_17_saida_desloca, celula_operacoes_17_transporte_saida_____b_out, celula_operacoes_17_transporte_saida_____c_out, and_1_out);
  comparador comparador_1 (.in_1(A), .in_2(B), .out_3(sao_iguais));

  // Notes on the sheet:
  //   overflow comp 2
  //   underflow [-]
  //   overflow [+] 
  //   overflow [+] comp 2 
  //   overflow desloca
  //   ULA
  //   Sistemas Digitais
  //   TADS 2014.1
  //   0 = and
  //   1 = or
  //   2 = xor
  //   3 = nand
  //   4 = somar
  //   5 = soma comp_2
  //   6 = subtrair
  //   7 = xnor
  //   8 = desloca
  //   9 = compara A < B
  //   Aluno: Renato F. Soares
endmodule

module comparador_novo (
  input  B,
  input  A,
  input  C_in,
  output C_out,
  output A___B
);

  wire and_1_out, not_1_out, xnor_1_out;

  not not_1 (not_1_out, A);
  xnor xnor_1 (xnor_1_out, A, B);
  and and_1 (and_1_out, not_1_out, B);
  and and_2 (C_out, C_in, xnor_1_out);
  and and_3 (A___B, C_in, and_1_out);

  // Notes on the sheet:
  //   CELULA COMPARADOR A<B
endmodule

module registrador (
  input  Dt31,
  input  Dt30,
  input  Dt29,
  input  Dt28,
  input  Dt27,
  input  Dt26,
  input  Dt25,
  input  Dt24,
  input  Dt23,
  input  Dt22,
  input  Dt21,
  input  Dt20,
  input  Dt19,
  input  Dt18,
  input  Dt17,
  input  Dt16,
  input  Dt15,
  input  Dt14,
  input  Dt13,
  input  Dt12,
  input  Dt11,
  input  Dt10,
  input  Dt09,
  input  Dt08,
  input  Dt07,
  input  Dt06,
  input  Dt05,
  input  Dt04,
  input  Dt03,
  input  Dt02,
  input  Dt01,
  input  Dt00,
  input  clear,
  input  write,
  output S31,
  output S30,
  output S29,
  output S28,
  output S27,
  output S26,
  output S25,
  output S24,
  output S23,
  output S22,
  output S21,
  output S20,
  output S19,
  output S18,
  output S17,
  output S16,
  output S15,
  output S14,
  output S13,
  output S12,
  output S11,
  output S10,
  output S09,
  output S08,
  output S07,
  output S06,
  output S05,
  output S04,
  output S03,
  output S02,
  output S01,
  output S00
);

  D_Flip_Flop d_ff_1 (.clk(write), .D(Dt31), .Q(S31), .reset(clear));  // open: Qn, preset, en
  D_Flip_Flop d_ff_2 (.clk(write), .D(Dt30), .Q(S30), .reset(clear));  // open: Qn, preset, en
  D_Flip_Flop d_ff_3 (.clk(write), .D(Dt29), .Q(S29), .reset(clear));  // open: Qn, preset, en
  D_Flip_Flop d_ff_4 (.clk(write), .D(Dt28), .Q(S28), .reset(clear));  // open: Qn, preset, en
  D_Flip_Flop d_ff_5 (.clk(write), .D(Dt27), .Q(S27), .reset(clear));  // open: Qn, preset, en
  D_Flip_Flop d_ff_6 (.clk(write), .D(Dt26), .Q(S26), .reset(clear));  // open: Qn, preset, en
  D_Flip_Flop d_ff_7 (.clk(write), .D(Dt25), .Q(S25), .reset(clear));  // open: Qn, preset, en
  D_Flip_Flop d_ff_8 (.clk(write), .D(Dt24), .Q(S24), .reset(clear));  // open: Qn, preset, en
  D_Flip_Flop d_ff_9 (.clk(write), .D(Dt23), .Q(S23), .reset(clear));  // open: Qn, preset, en
  D_Flip_Flop d_ff_10 (.clk(write), .D(Dt22), .Q(S22), .reset(clear));  // open: Qn, preset, en
  D_Flip_Flop d_ff_11 (.clk(write), .D(Dt21), .Q(S21), .reset(clear));  // open: Qn, preset, en
  D_Flip_Flop d_ff_12 (.clk(write), .D(Dt20), .Q(S20), .reset(clear));  // open: Qn, preset, en
  D_Flip_Flop d_ff_13 (.clk(write), .D(Dt19), .Q(S19), .reset(clear));  // open: Qn, preset, en
  D_Flip_Flop d_ff_14 (.clk(write), .D(Dt18), .Q(S18), .reset(clear));  // open: Qn, preset, en
  D_Flip_Flop d_ff_15 (.clk(write), .D(Dt17), .Q(S17), .reset(clear));  // open: Qn, preset, en
  D_Flip_Flop d_ff_16 (.clk(write), .D(Dt16), .Q(S16), .reset(clear));  // open: Qn, preset, en
  D_Flip_Flop d_ff_17 (.clk(write), .D(Dt15), .Q(S15), .reset(clear));  // open: Qn, preset, en
  D_Flip_Flop d_ff_18 (.clk(write), .D(Dt14), .Q(S14), .reset(clear));  // open: Qn, preset, en
  D_Flip_Flop d_ff_19 (.clk(write), .D(Dt13), .Q(S13), .reset(clear));  // open: Qn, preset, en
  D_Flip_Flop d_ff_20 (.clk(write), .D(Dt12), .Q(S12), .reset(clear));  // open: Qn, preset, en
  D_Flip_Flop d_ff_21 (.clk(write), .D(Dt11), .Q(S11), .reset(clear));  // open: Qn, preset, en
  D_Flip_Flop d_ff_22 (.clk(write), .D(Dt10), .Q(S10), .reset(clear));  // open: Qn, preset, en
  D_Flip_Flop d_ff_23 (.clk(write), .D(Dt09), .Q(S09), .reset(clear));  // open: Qn, preset, en
  D_Flip_Flop d_ff_24 (.clk(write), .D(Dt08), .Q(S08), .reset(clear));  // open: Qn, preset, en
  D_Flip_Flop d_ff_25 (.clk(write), .D(Dt07), .Q(S07), .reset(clear));  // open: Qn, preset, en
  D_Flip_Flop d_ff_26 (.clk(write), .D(Dt06), .Q(S06), .reset(clear));  // open: Qn, preset, en
  D_Flip_Flop d_ff_27 (.clk(write), .D(Dt05), .Q(S05), .reset(clear));  // open: Qn, preset, en
  D_Flip_Flop d_ff_28 (.clk(write), .D(Dt04), .Q(S04), .reset(clear));  // open: Qn, preset, en
  D_Flip_Flop d_ff_29 (.clk(write), .D(Dt03), .Q(S03), .reset(clear));  // open: Qn, preset, en
  D_Flip_Flop d_ff_30 (.clk(write), .D(Dt02), .Q(S02), .reset(clear));  // open: Qn, preset, en
  D_Flip_Flop d_ff_31 (.clk(write), .D(Dt01), .Q(S01), .reset(clear));  // open: Qn, preset, en
  D_Flip_Flop d_ff_32 (.clk(write), .D(Dt00), .Q(S00), .reset(clear));  // open: Qn, preset, en
endmodule

module banco_registrador (
  input  clear,
  input  [31:0] DATA_IN,
  input  [4:0] registrador_A,
  input  write,
  input  [4:0] \endereço_write ,
  input  [4:0] registrador_B,
  output [31:0] DATAreg_A,
  output [31:0] DATAreg_B
);

  wire demultiplexer_1_out0, demultiplexer_1_out1, demultiplexer_1_out2, demultiplexer_1_out3,
       demultiplexer_1_out4, demultiplexer_1_out5, demultiplexer_1_out6, demultiplexer_1_out7,
       demultiplexer_1_out8, demultiplexer_1_out9, demultiplexer_1_out10, demultiplexer_1_out11,
       demultiplexer_1_out12, demultiplexer_1_out13, demultiplexer_1_out14, demultiplexer_1_out15,
       demultiplexer_1_out16, demultiplexer_1_out17, demultiplexer_1_out18, demultiplexer_1_out19,
       demultiplexer_1_out20, demultiplexer_1_out21, demultiplexer_1_out22, demultiplexer_1_out23,
       demultiplexer_1_out24, demultiplexer_1_out25, demultiplexer_1_out26, demultiplexer_1_out27,
       demultiplexer_1_out28, demultiplexer_1_out29, demultiplexer_1_out30, demultiplexer_1_out31;
  wire [31:0] _00000_s00, _00001_s00, _00010_s00, _00011_s00, _00100_s00, _00101_s00, registrador_1_s00,
       registrador_2_s00, registrador_3_s00, registrador_4_s00, registrador_5_s00, registrador_6_s00,
       registrador_7_s00, registrador_8_s00, registrador_9_s00, registrador_10_s00, registrador_11_s00,
       registrador_12_s00, registrador_13_s00, registrador_14_s00, registrador_15_s00, registrador_16_s00,
       registrador_17_s00, registrador_18_s00, registrador_19_s00, registrador_20_s00, registrador_21_s00,
       registrador_22_s00, registrador_23_s00, registrador_24_s00, registrador_25_s00, registrador_26_s00;

  Demultiplexer #(.select(5), .enable("false")) demultiplexer_1 (
    .out0(demultiplexer_1_out0), .out1(demultiplexer_1_out1), .out2(demultiplexer_1_out2),
    .out3(demultiplexer_1_out3), .out4(demultiplexer_1_out4), .out5(demultiplexer_1_out5),
    .out6(demultiplexer_1_out6), .out7(demultiplexer_1_out7), .out8(demultiplexer_1_out8),
    .out9(demultiplexer_1_out9), .out10(demultiplexer_1_out10), .out11(demultiplexer_1_out11),
    .out12(demultiplexer_1_out12), .out13(demultiplexer_1_out13), .out14(demultiplexer_1_out14),
    .out15(demultiplexer_1_out15), .out16(demultiplexer_1_out16), .out17(demultiplexer_1_out17),
    .out18(demultiplexer_1_out18), .out19(demultiplexer_1_out19), .out20(demultiplexer_1_out20),
    .out21(demultiplexer_1_out21), .out22(demultiplexer_1_out22), .out23(demultiplexer_1_out23),
    .out24(demultiplexer_1_out24), .out25(demultiplexer_1_out25), .out26(demultiplexer_1_out26),
    .out27(demultiplexer_1_out27), .out28(demultiplexer_1_out28), .out29(demultiplexer_1_out29),
    .out30(demultiplexer_1_out30), .out31(demultiplexer_1_out31), .in(write), .sel(\endereço_write ));
  registrador _00000 (
    .write(demultiplexer_1_out0), .clear(clear), .Dt31(DATA_IN[31]), .Dt30(DATA_IN[30]), .Dt29(DATA_IN[29]),
    .Dt28(DATA_IN[28]), .Dt27(DATA_IN[27]), .Dt26(DATA_IN[26]), .Dt25(DATA_IN[25]), .Dt24(DATA_IN[24]),
    .Dt23(DATA_IN[23]), .Dt22(DATA_IN[22]), .Dt21(DATA_IN[21]), .Dt20(DATA_IN[20]), .Dt19(DATA_IN[19]),
    .Dt18(DATA_IN[18]), .Dt17(DATA_IN[17]), .Dt16(DATA_IN[16]), .Dt15(DATA_IN[15]), .Dt14(DATA_IN[14]),
    .Dt13(DATA_IN[13]), .Dt12(DATA_IN[12]), .Dt11(DATA_IN[11]), .Dt10(DATA_IN[10]), .Dt09(DATA_IN[9]),
    .Dt08(DATA_IN[8]), .Dt07(DATA_IN[7]), .Dt06(DATA_IN[6]), .Dt05(DATA_IN[5]), .Dt04(DATA_IN[4]),
    .Dt03(DATA_IN[3]), .Dt02(DATA_IN[2]), .Dt01(DATA_IN[1]), .Dt00(DATA_IN[0]), .S31(_00000_s00[31]),
    .S30(_00000_s00[30]), .S29(_00000_s00[29]), .S28(_00000_s00[28]), .S27(_00000_s00[27]),
    .S26(_00000_s00[26]), .S25(_00000_s00[25]), .S24(_00000_s00[24]), .S23(_00000_s00[23]),
    .S22(_00000_s00[22]), .S21(_00000_s00[21]), .S20(_00000_s00[20]), .S19(_00000_s00[19]),
    .S18(_00000_s00[18]), .S17(_00000_s00[17]), .S16(_00000_s00[16]), .S15(_00000_s00[15]),
    .S14(_00000_s00[14]), .S13(_00000_s00[13]), .S12(_00000_s00[12]), .S11(_00000_s00[11]),
    .S10(_00000_s00[10]), .S09(_00000_s00[9]), .S08(_00000_s00[8]), .S07(_00000_s00[7]), .S06(_00000_s00[6]),
    .S05(_00000_s00[5]), .S04(_00000_s00[4]), .S03(_00000_s00[3]), .S02(_00000_s00[2]), .S01(_00000_s00[1]),
    .S00(_00000_s00[0]));
  registrador _00001 (
    .write(demultiplexer_1_out1), .clear(clear), .Dt31(DATA_IN[31]), .Dt30(DATA_IN[30]), .Dt29(DATA_IN[29]),
    .Dt28(DATA_IN[28]), .Dt27(DATA_IN[27]), .Dt26(DATA_IN[26]), .Dt25(DATA_IN[25]), .Dt24(DATA_IN[24]),
    .Dt23(DATA_IN[23]), .Dt22(DATA_IN[22]), .Dt21(DATA_IN[21]), .Dt20(DATA_IN[20]), .Dt19(DATA_IN[19]),
    .Dt18(DATA_IN[18]), .Dt17(DATA_IN[17]), .Dt16(DATA_IN[16]), .Dt15(DATA_IN[15]), .Dt14(DATA_IN[14]),
    .Dt13(DATA_IN[13]), .Dt12(DATA_IN[12]), .Dt11(DATA_IN[11]), .Dt10(DATA_IN[10]), .Dt09(DATA_IN[9]),
    .Dt08(DATA_IN[8]), .Dt07(DATA_IN[7]), .Dt06(DATA_IN[6]), .Dt05(DATA_IN[5]), .Dt04(DATA_IN[4]),
    .Dt03(DATA_IN[3]), .Dt02(DATA_IN[2]), .Dt01(DATA_IN[1]), .Dt00(DATA_IN[0]), .S31(_00001_s00[31]),
    .S30(_00001_s00[30]), .S29(_00001_s00[29]), .S28(_00001_s00[28]), .S27(_00001_s00[27]),
    .S26(_00001_s00[26]), .S25(_00001_s00[25]), .S24(_00001_s00[24]), .S23(_00001_s00[23]),
    .S22(_00001_s00[22]), .S21(_00001_s00[21]), .S20(_00001_s00[20]), .S19(_00001_s00[19]),
    .S18(_00001_s00[18]), .S17(_00001_s00[17]), .S16(_00001_s00[16]), .S15(_00001_s00[15]),
    .S14(_00001_s00[14]), .S13(_00001_s00[13]), .S12(_00001_s00[12]), .S11(_00001_s00[11]),
    .S10(_00001_s00[10]), .S09(_00001_s00[9]), .S08(_00001_s00[8]), .S07(_00001_s00[7]), .S06(_00001_s00[6]),
    .S05(_00001_s00[5]), .S04(_00001_s00[4]), .S03(_00001_s00[3]), .S02(_00001_s00[2]), .S01(_00001_s00[1]),
    .S00(_00001_s00[0]));
  registrador _00010 (
    .write(demultiplexer_1_out2), .clear(clear), .Dt31(DATA_IN[31]), .Dt30(DATA_IN[30]), .Dt29(DATA_IN[29]),
    .Dt28(DATA_IN[28]), .Dt27(DATA_IN[27]), .Dt26(DATA_IN[26]), .Dt25(DATA_IN[25]), .Dt24(DATA_IN[24]),
    .Dt23(DATA_IN[23]), .Dt22(DATA_IN[22]), .Dt21(DATA_IN[21]), .Dt20(DATA_IN[20]), .Dt19(DATA_IN[19]),
    .Dt18(DATA_IN[18]), .Dt17(DATA_IN[17]), .Dt16(DATA_IN[16]), .Dt15(DATA_IN[15]), .Dt14(DATA_IN[14]),
    .Dt13(DATA_IN[13]), .Dt12(DATA_IN[12]), .Dt11(DATA_IN[11]), .Dt10(DATA_IN[10]), .Dt09(DATA_IN[9]),
    .Dt08(DATA_IN[8]), .Dt07(DATA_IN[7]), .Dt06(DATA_IN[6]), .Dt05(DATA_IN[5]), .Dt04(DATA_IN[4]),
    .Dt03(DATA_IN[3]), .Dt02(DATA_IN[2]), .Dt01(DATA_IN[1]), .Dt00(DATA_IN[0]), .S31(_00010_s00[31]),
    .S30(_00010_s00[30]), .S29(_00010_s00[29]), .S28(_00010_s00[28]), .S27(_00010_s00[27]),
    .S26(_00010_s00[26]), .S25(_00010_s00[25]), .S24(_00010_s00[24]), .S23(_00010_s00[23]),
    .S22(_00010_s00[22]), .S21(_00010_s00[21]), .S20(_00010_s00[20]), .S19(_00010_s00[19]),
    .S18(_00010_s00[18]), .S17(_00010_s00[17]), .S16(_00010_s00[16]), .S15(_00010_s00[15]),
    .S14(_00010_s00[14]), .S13(_00010_s00[13]), .S12(_00010_s00[12]), .S11(_00010_s00[11]),
    .S10(_00010_s00[10]), .S09(_00010_s00[9]), .S08(_00010_s00[8]), .S07(_00010_s00[7]), .S06(_00010_s00[6]),
    .S05(_00010_s00[5]), .S04(_00010_s00[4]), .S03(_00010_s00[3]), .S02(_00010_s00[2]), .S01(_00010_s00[1]),
    .S00(_00010_s00[0]));
  registrador _00011 (
    .write(demultiplexer_1_out3), .clear(clear), .Dt31(DATA_IN[31]), .Dt30(DATA_IN[30]), .Dt29(DATA_IN[29]),
    .Dt28(DATA_IN[28]), .Dt27(DATA_IN[27]), .Dt26(DATA_IN[26]), .Dt25(DATA_IN[25]), .Dt24(DATA_IN[24]),
    .Dt23(DATA_IN[23]), .Dt22(DATA_IN[22]), .Dt21(DATA_IN[21]), .Dt20(DATA_IN[20]), .Dt19(DATA_IN[19]),
    .Dt18(DATA_IN[18]), .Dt17(DATA_IN[17]), .Dt16(DATA_IN[16]), .Dt15(DATA_IN[15]), .Dt14(DATA_IN[14]),
    .Dt13(DATA_IN[13]), .Dt12(DATA_IN[12]), .Dt11(DATA_IN[11]), .Dt10(DATA_IN[10]), .Dt09(DATA_IN[9]),
    .Dt08(DATA_IN[8]), .Dt07(DATA_IN[7]), .Dt06(DATA_IN[6]), .Dt05(DATA_IN[5]), .Dt04(DATA_IN[4]),
    .Dt03(DATA_IN[3]), .Dt02(DATA_IN[2]), .Dt01(DATA_IN[1]), .Dt00(DATA_IN[0]), .S31(_00011_s00[31]),
    .S30(_00011_s00[30]), .S29(_00011_s00[29]), .S28(_00011_s00[28]), .S27(_00011_s00[27]),
    .S26(_00011_s00[26]), .S25(_00011_s00[25]), .S24(_00011_s00[24]), .S23(_00011_s00[23]),
    .S22(_00011_s00[22]), .S21(_00011_s00[21]), .S20(_00011_s00[20]), .S19(_00011_s00[19]),
    .S18(_00011_s00[18]), .S17(_00011_s00[17]), .S16(_00011_s00[16]), .S15(_00011_s00[15]),
    .S14(_00011_s00[14]), .S13(_00011_s00[13]), .S12(_00011_s00[12]), .S11(_00011_s00[11]),
    .S10(_00011_s00[10]), .S09(_00011_s00[9]), .S08(_00011_s00[8]), .S07(_00011_s00[7]), .S06(_00011_s00[6]),
    .S05(_00011_s00[5]), .S04(_00011_s00[4]), .S03(_00011_s00[3]), .S02(_00011_s00[2]), .S01(_00011_s00[1]),
    .S00(_00011_s00[0]));
  registrador _00100 (
    .write(demultiplexer_1_out4), .clear(clear), .Dt31(DATA_IN[31]), .Dt30(DATA_IN[30]), .Dt29(DATA_IN[29]),
    .Dt28(DATA_IN[28]), .Dt27(DATA_IN[27]), .Dt26(DATA_IN[26]), .Dt25(DATA_IN[25]), .Dt24(DATA_IN[24]),
    .Dt23(DATA_IN[23]), .Dt22(DATA_IN[22]), .Dt21(DATA_IN[21]), .Dt20(DATA_IN[20]), .Dt19(DATA_IN[19]),
    .Dt18(DATA_IN[18]), .Dt17(DATA_IN[17]), .Dt16(DATA_IN[16]), .Dt15(DATA_IN[15]), .Dt14(DATA_IN[14]),
    .Dt13(DATA_IN[13]), .Dt12(DATA_IN[12]), .Dt11(DATA_IN[11]), .Dt10(DATA_IN[10]), .Dt09(DATA_IN[9]),
    .Dt08(DATA_IN[8]), .Dt07(DATA_IN[7]), .Dt06(DATA_IN[6]), .Dt05(DATA_IN[5]), .Dt04(DATA_IN[4]),
    .Dt03(DATA_IN[3]), .Dt02(DATA_IN[2]), .Dt01(DATA_IN[1]), .Dt00(DATA_IN[0]), .S31(_00100_s00[31]),
    .S30(_00100_s00[30]), .S29(_00100_s00[29]), .S28(_00100_s00[28]), .S27(_00100_s00[27]),
    .S26(_00100_s00[26]), .S25(_00100_s00[25]), .S24(_00100_s00[24]), .S23(_00100_s00[23]),
    .S22(_00100_s00[22]), .S21(_00100_s00[21]), .S20(_00100_s00[20]), .S19(_00100_s00[19]),
    .S18(_00100_s00[18]), .S17(_00100_s00[17]), .S16(_00100_s00[16]), .S15(_00100_s00[15]),
    .S14(_00100_s00[14]), .S13(_00100_s00[13]), .S12(_00100_s00[12]), .S11(_00100_s00[11]),
    .S10(_00100_s00[10]), .S09(_00100_s00[9]), .S08(_00100_s00[8]), .S07(_00100_s00[7]), .S06(_00100_s00[6]),
    .S05(_00100_s00[5]), .S04(_00100_s00[4]), .S03(_00100_s00[3]), .S02(_00100_s00[2]), .S01(_00100_s00[1]),
    .S00(_00100_s00[0]));
  registrador _00101 (
    .write(demultiplexer_1_out5), .clear(clear), .Dt31(DATA_IN[31]), .Dt30(DATA_IN[30]), .Dt29(DATA_IN[29]),
    .Dt28(DATA_IN[28]), .Dt27(DATA_IN[27]), .Dt26(DATA_IN[26]), .Dt25(DATA_IN[25]), .Dt24(DATA_IN[24]),
    .Dt23(DATA_IN[23]), .Dt22(DATA_IN[22]), .Dt21(DATA_IN[21]), .Dt20(DATA_IN[20]), .Dt19(DATA_IN[19]),
    .Dt18(DATA_IN[18]), .Dt17(DATA_IN[17]), .Dt16(DATA_IN[16]), .Dt15(DATA_IN[15]), .Dt14(DATA_IN[14]),
    .Dt13(DATA_IN[13]), .Dt12(DATA_IN[12]), .Dt11(DATA_IN[11]), .Dt10(DATA_IN[10]), .Dt09(DATA_IN[9]),
    .Dt08(DATA_IN[8]), .Dt07(DATA_IN[7]), .Dt06(DATA_IN[6]), .Dt05(DATA_IN[5]), .Dt04(DATA_IN[4]),
    .Dt03(DATA_IN[3]), .Dt02(DATA_IN[2]), .Dt01(DATA_IN[1]), .Dt00(DATA_IN[0]), .S31(_00101_s00[31]),
    .S30(_00101_s00[30]), .S29(_00101_s00[29]), .S28(_00101_s00[28]), .S27(_00101_s00[27]),
    .S26(_00101_s00[26]), .S25(_00101_s00[25]), .S24(_00101_s00[24]), .S23(_00101_s00[23]),
    .S22(_00101_s00[22]), .S21(_00101_s00[21]), .S20(_00101_s00[20]), .S19(_00101_s00[19]),
    .S18(_00101_s00[18]), .S17(_00101_s00[17]), .S16(_00101_s00[16]), .S15(_00101_s00[15]),
    .S14(_00101_s00[14]), .S13(_00101_s00[13]), .S12(_00101_s00[12]), .S11(_00101_s00[11]),
    .S10(_00101_s00[10]), .S09(_00101_s00[9]), .S08(_00101_s00[8]), .S07(_00101_s00[7]), .S06(_00101_s00[6]),
    .S05(_00101_s00[5]), .S04(_00101_s00[4]), .S03(_00101_s00[3]), .S02(_00101_s00[2]), .S01(_00101_s00[1]),
    .S00(_00101_s00[0]));
  registrador registrador_1 (
    .write(demultiplexer_1_out6), .clear(clear), .Dt31(DATA_IN[31]), .Dt30(DATA_IN[30]), .Dt29(DATA_IN[29]),
    .Dt28(DATA_IN[28]), .Dt27(DATA_IN[27]), .Dt26(DATA_IN[26]), .Dt25(DATA_IN[25]), .Dt24(DATA_IN[24]),
    .Dt23(DATA_IN[23]), .Dt22(DATA_IN[22]), .Dt21(DATA_IN[21]), .Dt20(DATA_IN[20]), .Dt19(DATA_IN[19]),
    .Dt18(DATA_IN[18]), .Dt17(DATA_IN[17]), .Dt16(DATA_IN[16]), .Dt15(DATA_IN[15]), .Dt14(DATA_IN[14]),
    .Dt13(DATA_IN[13]), .Dt12(DATA_IN[12]), .Dt11(DATA_IN[11]), .Dt10(DATA_IN[10]), .Dt09(DATA_IN[9]),
    .Dt08(DATA_IN[8]), .Dt07(DATA_IN[7]), .Dt06(DATA_IN[6]), .Dt05(DATA_IN[5]), .Dt04(DATA_IN[4]),
    .Dt03(DATA_IN[3]), .Dt02(DATA_IN[2]), .Dt01(DATA_IN[1]), .Dt00(DATA_IN[0]), .S31(registrador_1_s00[31]),
    .S30(registrador_1_s00[30]), .S29(registrador_1_s00[29]), .S28(registrador_1_s00[28]),
    .S27(registrador_1_s00[27]), .S26(registrador_1_s00[26]), .S25(registrador_1_s00[25]),
    .S24(registrador_1_s00[24]), .S23(registrador_1_s00[23]), .S22(registrador_1_s00[22]),
    .S21(registrador_1_s00[21]), .S20(registrador_1_s00[20]), .S19(registrador_1_s00[19]),
    .S18(registrador_1_s00[18]), .S17(registrador_1_s00[17]), .S16(registrador_1_s00[16]),
    .S15(registrador_1_s00[15]), .S14(registrador_1_s00[14]), .S13(registrador_1_s00[13]),
    .S12(registrador_1_s00[12]), .S11(registrador_1_s00[11]), .S10(registrador_1_s00[10]),
    .S09(registrador_1_s00[9]), .S08(registrador_1_s00[8]), .S07(registrador_1_s00[7]),
    .S06(registrador_1_s00[6]), .S05(registrador_1_s00[5]), .S04(registrador_1_s00[4]),
    .S03(registrador_1_s00[3]), .S02(registrador_1_s00[2]), .S01(registrador_1_s00[1]),
    .S00(registrador_1_s00[0]));
  registrador registrador_2 (
    .write(demultiplexer_1_out7), .clear(clear), .Dt31(DATA_IN[31]), .Dt30(DATA_IN[30]), .Dt29(DATA_IN[29]),
    .Dt28(DATA_IN[28]), .Dt27(DATA_IN[27]), .Dt26(DATA_IN[26]), .Dt25(DATA_IN[25]), .Dt24(DATA_IN[24]),
    .Dt23(DATA_IN[23]), .Dt22(DATA_IN[22]), .Dt21(DATA_IN[21]), .Dt20(DATA_IN[20]), .Dt19(DATA_IN[19]),
    .Dt18(DATA_IN[18]), .Dt17(DATA_IN[17]), .Dt16(DATA_IN[16]), .Dt15(DATA_IN[15]), .Dt14(DATA_IN[14]),
    .Dt13(DATA_IN[13]), .Dt12(DATA_IN[12]), .Dt11(DATA_IN[11]), .Dt10(DATA_IN[10]), .Dt09(DATA_IN[9]),
    .Dt08(DATA_IN[8]), .Dt07(DATA_IN[7]), .Dt06(DATA_IN[6]), .Dt05(DATA_IN[5]), .Dt04(DATA_IN[4]),
    .Dt03(DATA_IN[3]), .Dt02(DATA_IN[2]), .Dt01(DATA_IN[1]), .Dt00(DATA_IN[0]), .S31(registrador_2_s00[31]),
    .S30(registrador_2_s00[30]), .S29(registrador_2_s00[29]), .S28(registrador_2_s00[28]),
    .S27(registrador_2_s00[27]), .S26(registrador_2_s00[26]), .S25(registrador_2_s00[25]),
    .S24(registrador_2_s00[24]), .S23(registrador_2_s00[23]), .S22(registrador_2_s00[22]),
    .S21(registrador_2_s00[21]), .S20(registrador_2_s00[20]), .S19(registrador_2_s00[19]),
    .S18(registrador_2_s00[18]), .S17(registrador_2_s00[17]), .S16(registrador_2_s00[16]),
    .S15(registrador_2_s00[15]), .S14(registrador_2_s00[14]), .S13(registrador_2_s00[13]),
    .S12(registrador_2_s00[12]), .S11(registrador_2_s00[11]), .S10(registrador_2_s00[10]),
    .S09(registrador_2_s00[9]), .S08(registrador_2_s00[8]), .S07(registrador_2_s00[7]),
    .S06(registrador_2_s00[6]), .S05(registrador_2_s00[5]), .S04(registrador_2_s00[4]),
    .S03(registrador_2_s00[3]), .S02(registrador_2_s00[2]), .S01(registrador_2_s00[1]),
    .S00(registrador_2_s00[0]));
  registrador registrador_3 (
    .write(demultiplexer_1_out8), .clear(clear), .Dt31(DATA_IN[31]), .Dt30(DATA_IN[30]), .Dt29(DATA_IN[29]),
    .Dt28(DATA_IN[28]), .Dt27(DATA_IN[27]), .Dt26(DATA_IN[26]), .Dt25(DATA_IN[25]), .Dt24(DATA_IN[24]),
    .Dt23(DATA_IN[23]), .Dt22(DATA_IN[22]), .Dt21(DATA_IN[21]), .Dt20(DATA_IN[20]), .Dt19(DATA_IN[19]),
    .Dt18(DATA_IN[18]), .Dt17(DATA_IN[17]), .Dt16(DATA_IN[16]), .Dt15(DATA_IN[15]), .Dt14(DATA_IN[14]),
    .Dt13(DATA_IN[13]), .Dt12(DATA_IN[12]), .Dt11(DATA_IN[11]), .Dt10(DATA_IN[10]), .Dt09(DATA_IN[9]),
    .Dt08(DATA_IN[8]), .Dt07(DATA_IN[7]), .Dt06(DATA_IN[6]), .Dt05(DATA_IN[5]), .Dt04(DATA_IN[4]),
    .Dt03(DATA_IN[3]), .Dt02(DATA_IN[2]), .Dt01(DATA_IN[1]), .Dt00(DATA_IN[0]), .S31(registrador_3_s00[31]),
    .S30(registrador_3_s00[30]), .S29(registrador_3_s00[29]), .S28(registrador_3_s00[28]),
    .S27(registrador_3_s00[27]), .S26(registrador_3_s00[26]), .S25(registrador_3_s00[25]),
    .S24(registrador_3_s00[24]), .S23(registrador_3_s00[23]), .S22(registrador_3_s00[22]),
    .S21(registrador_3_s00[21]), .S20(registrador_3_s00[20]), .S19(registrador_3_s00[19]),
    .S18(registrador_3_s00[18]), .S17(registrador_3_s00[17]), .S16(registrador_3_s00[16]),
    .S15(registrador_3_s00[15]), .S14(registrador_3_s00[14]), .S13(registrador_3_s00[13]),
    .S12(registrador_3_s00[12]), .S11(registrador_3_s00[11]), .S10(registrador_3_s00[10]),
    .S09(registrador_3_s00[9]), .S08(registrador_3_s00[8]), .S07(registrador_3_s00[7]),
    .S06(registrador_3_s00[6]), .S05(registrador_3_s00[5]), .S04(registrador_3_s00[4]),
    .S03(registrador_3_s00[3]), .S02(registrador_3_s00[2]), .S01(registrador_3_s00[1]),
    .S00(registrador_3_s00[0]));
  registrador registrador_4 (
    .write(demultiplexer_1_out9), .clear(clear), .Dt31(DATA_IN[31]), .Dt30(DATA_IN[30]), .Dt29(DATA_IN[29]),
    .Dt28(DATA_IN[28]), .Dt27(DATA_IN[27]), .Dt26(DATA_IN[26]), .Dt25(DATA_IN[25]), .Dt24(DATA_IN[24]),
    .Dt23(DATA_IN[23]), .Dt22(DATA_IN[22]), .Dt21(DATA_IN[21]), .Dt20(DATA_IN[20]), .Dt19(DATA_IN[19]),
    .Dt18(DATA_IN[18]), .Dt17(DATA_IN[17]), .Dt16(DATA_IN[16]), .Dt15(DATA_IN[15]), .Dt14(DATA_IN[14]),
    .Dt13(DATA_IN[13]), .Dt12(DATA_IN[12]), .Dt11(DATA_IN[11]), .Dt10(DATA_IN[10]), .Dt09(DATA_IN[9]),
    .Dt08(DATA_IN[8]), .Dt07(DATA_IN[7]), .Dt06(DATA_IN[6]), .Dt05(DATA_IN[5]), .Dt04(DATA_IN[4]),
    .Dt03(DATA_IN[3]), .Dt02(DATA_IN[2]), .Dt01(DATA_IN[1]), .Dt00(DATA_IN[0]), .S31(registrador_4_s00[31]),
    .S30(registrador_4_s00[30]), .S29(registrador_4_s00[29]), .S28(registrador_4_s00[28]),
    .S27(registrador_4_s00[27]), .S26(registrador_4_s00[26]), .S25(registrador_4_s00[25]),
    .S24(registrador_4_s00[24]), .S23(registrador_4_s00[23]), .S22(registrador_4_s00[22]),
    .S21(registrador_4_s00[21]), .S20(registrador_4_s00[20]), .S19(registrador_4_s00[19]),
    .S18(registrador_4_s00[18]), .S17(registrador_4_s00[17]), .S16(registrador_4_s00[16]),
    .S15(registrador_4_s00[15]), .S14(registrador_4_s00[14]), .S13(registrador_4_s00[13]),
    .S12(registrador_4_s00[12]), .S11(registrador_4_s00[11]), .S10(registrador_4_s00[10]),
    .S09(registrador_4_s00[9]), .S08(registrador_4_s00[8]), .S07(registrador_4_s00[7]),
    .S06(registrador_4_s00[6]), .S05(registrador_4_s00[5]), .S04(registrador_4_s00[4]),
    .S03(registrador_4_s00[3]), .S02(registrador_4_s00[2]), .S01(registrador_4_s00[1]),
    .S00(registrador_4_s00[0]));
  registrador registrador_5 (
    .write(demultiplexer_1_out10), .clear(clear), .Dt31(DATA_IN[31]), .Dt30(DATA_IN[30]), .Dt29(DATA_IN[29]),
    .Dt28(DATA_IN[28]), .Dt27(DATA_IN[27]), .Dt26(DATA_IN[26]), .Dt25(DATA_IN[25]), .Dt24(DATA_IN[24]),
    .Dt23(DATA_IN[23]), .Dt22(DATA_IN[22]), .Dt21(DATA_IN[21]), .Dt20(DATA_IN[20]), .Dt19(DATA_IN[19]),
    .Dt18(DATA_IN[18]), .Dt17(DATA_IN[17]), .Dt16(DATA_IN[16]), .Dt15(DATA_IN[15]), .Dt14(DATA_IN[14]),
    .Dt13(DATA_IN[13]), .Dt12(DATA_IN[12]), .Dt11(DATA_IN[11]), .Dt10(DATA_IN[10]), .Dt09(DATA_IN[9]),
    .Dt08(DATA_IN[8]), .Dt07(DATA_IN[7]), .Dt06(DATA_IN[6]), .Dt05(DATA_IN[5]), .Dt04(DATA_IN[4]),
    .Dt03(DATA_IN[3]), .Dt02(DATA_IN[2]), .Dt01(DATA_IN[1]), .Dt00(DATA_IN[0]), .S31(registrador_5_s00[31]),
    .S30(registrador_5_s00[30]), .S29(registrador_5_s00[29]), .S28(registrador_5_s00[28]),
    .S27(registrador_5_s00[27]), .S26(registrador_5_s00[26]), .S25(registrador_5_s00[25]),
    .S24(registrador_5_s00[24]), .S23(registrador_5_s00[23]), .S22(registrador_5_s00[22]),
    .S21(registrador_5_s00[21]), .S20(registrador_5_s00[20]), .S19(registrador_5_s00[19]),
    .S18(registrador_5_s00[18]), .S17(registrador_5_s00[17]), .S16(registrador_5_s00[16]),
    .S15(registrador_5_s00[15]), .S14(registrador_5_s00[14]), .S13(registrador_5_s00[13]),
    .S12(registrador_5_s00[12]), .S11(registrador_5_s00[11]), .S10(registrador_5_s00[10]),
    .S09(registrador_5_s00[9]), .S08(registrador_5_s00[8]), .S07(registrador_5_s00[7]),
    .S06(registrador_5_s00[6]), .S05(registrador_5_s00[5]), .S04(registrador_5_s00[4]),
    .S03(registrador_5_s00[3]), .S02(registrador_5_s00[2]), .S01(registrador_5_s00[1]),
    .S00(registrador_5_s00[0]));
  registrador registrador_6 (
    .write(demultiplexer_1_out11), .clear(clear), .Dt31(DATA_IN[31]), .Dt30(DATA_IN[30]), .Dt29(DATA_IN[29]),
    .Dt28(DATA_IN[28]), .Dt27(DATA_IN[27]), .Dt26(DATA_IN[26]), .Dt25(DATA_IN[25]), .Dt24(DATA_IN[24]),
    .Dt23(DATA_IN[23]), .Dt22(DATA_IN[22]), .Dt21(DATA_IN[21]), .Dt20(DATA_IN[20]), .Dt19(DATA_IN[19]),
    .Dt18(DATA_IN[18]), .Dt17(DATA_IN[17]), .Dt16(DATA_IN[16]), .Dt15(DATA_IN[15]), .Dt14(DATA_IN[14]),
    .Dt13(DATA_IN[13]), .Dt12(DATA_IN[12]), .Dt11(DATA_IN[11]), .Dt10(DATA_IN[10]), .Dt09(DATA_IN[9]),
    .Dt08(DATA_IN[8]), .Dt07(DATA_IN[7]), .Dt06(DATA_IN[6]), .Dt05(DATA_IN[5]), .Dt04(DATA_IN[4]),
    .Dt03(DATA_IN[3]), .Dt02(DATA_IN[2]), .Dt01(DATA_IN[1]), .Dt00(DATA_IN[0]), .S31(registrador_6_s00[31]),
    .S30(registrador_6_s00[30]), .S29(registrador_6_s00[29]), .S28(registrador_6_s00[28]),
    .S27(registrador_6_s00[27]), .S26(registrador_6_s00[26]), .S25(registrador_6_s00[25]),
    .S24(registrador_6_s00[24]), .S23(registrador_6_s00[23]), .S22(registrador_6_s00[22]),
    .S21(registrador_6_s00[21]), .S20(registrador_6_s00[20]), .S19(registrador_6_s00[19]),
    .S18(registrador_6_s00[18]), .S17(registrador_6_s00[17]), .S16(registrador_6_s00[16]),
    .S15(registrador_6_s00[15]), .S14(registrador_6_s00[14]), .S13(registrador_6_s00[13]),
    .S12(registrador_6_s00[12]), .S11(registrador_6_s00[11]), .S10(registrador_6_s00[10]),
    .S09(registrador_6_s00[9]), .S08(registrador_6_s00[8]), .S07(registrador_6_s00[7]),
    .S06(registrador_6_s00[6]), .S05(registrador_6_s00[5]), .S04(registrador_6_s00[4]),
    .S03(registrador_6_s00[3]), .S02(registrador_6_s00[2]), .S01(registrador_6_s00[1]),
    .S00(registrador_6_s00[0]));
  registrador registrador_7 (
    .write(demultiplexer_1_out12), .clear(clear), .Dt31(DATA_IN[31]), .Dt30(DATA_IN[30]), .Dt29(DATA_IN[29]),
    .Dt28(DATA_IN[28]), .Dt27(DATA_IN[27]), .Dt26(DATA_IN[26]), .Dt25(DATA_IN[25]), .Dt24(DATA_IN[24]),
    .Dt23(DATA_IN[23]), .Dt22(DATA_IN[22]), .Dt21(DATA_IN[21]), .Dt20(DATA_IN[20]), .Dt19(DATA_IN[19]),
    .Dt18(DATA_IN[18]), .Dt17(DATA_IN[17]), .Dt16(DATA_IN[16]), .Dt15(DATA_IN[15]), .Dt14(DATA_IN[14]),
    .Dt13(DATA_IN[13]), .Dt12(DATA_IN[12]), .Dt11(DATA_IN[11]), .Dt10(DATA_IN[10]), .Dt09(DATA_IN[9]),
    .Dt08(DATA_IN[8]), .Dt07(DATA_IN[7]), .Dt06(DATA_IN[6]), .Dt05(DATA_IN[5]), .Dt04(DATA_IN[4]),
    .Dt03(DATA_IN[3]), .Dt02(DATA_IN[2]), .Dt01(DATA_IN[1]), .Dt00(DATA_IN[0]), .S31(registrador_7_s00[31]),
    .S30(registrador_7_s00[30]), .S29(registrador_7_s00[29]), .S28(registrador_7_s00[28]),
    .S27(registrador_7_s00[27]), .S26(registrador_7_s00[26]), .S25(registrador_7_s00[25]),
    .S24(registrador_7_s00[24]), .S23(registrador_7_s00[23]), .S22(registrador_7_s00[22]),
    .S21(registrador_7_s00[21]), .S20(registrador_7_s00[20]), .S19(registrador_7_s00[19]),
    .S18(registrador_7_s00[18]), .S17(registrador_7_s00[17]), .S16(registrador_7_s00[16]),
    .S15(registrador_7_s00[15]), .S14(registrador_7_s00[14]), .S13(registrador_7_s00[13]),
    .S12(registrador_7_s00[12]), .S11(registrador_7_s00[11]), .S10(registrador_7_s00[10]),
    .S09(registrador_7_s00[9]), .S08(registrador_7_s00[8]), .S07(registrador_7_s00[7]),
    .S06(registrador_7_s00[6]), .S05(registrador_7_s00[5]), .S04(registrador_7_s00[4]),
    .S03(registrador_7_s00[3]), .S02(registrador_7_s00[2]), .S01(registrador_7_s00[1]),
    .S00(registrador_7_s00[0]));
  registrador registrador_8 (
    .write(demultiplexer_1_out13), .clear(clear), .Dt31(DATA_IN[31]), .Dt30(DATA_IN[30]), .Dt29(DATA_IN[29]),
    .Dt28(DATA_IN[28]), .Dt27(DATA_IN[27]), .Dt26(DATA_IN[26]), .Dt25(DATA_IN[25]), .Dt24(DATA_IN[24]),
    .Dt23(DATA_IN[23]), .Dt22(DATA_IN[22]), .Dt21(DATA_IN[21]), .Dt20(DATA_IN[20]), .Dt19(DATA_IN[19]),
    .Dt18(DATA_IN[18]), .Dt17(DATA_IN[17]), .Dt16(DATA_IN[16]), .Dt15(DATA_IN[15]), .Dt14(DATA_IN[14]),
    .Dt13(DATA_IN[13]), .Dt12(DATA_IN[12]), .Dt11(DATA_IN[11]), .Dt10(DATA_IN[10]), .Dt09(DATA_IN[9]),
    .Dt08(DATA_IN[8]), .Dt07(DATA_IN[7]), .Dt06(DATA_IN[6]), .Dt05(DATA_IN[5]), .Dt04(DATA_IN[4]),
    .Dt03(DATA_IN[3]), .Dt02(DATA_IN[2]), .Dt01(DATA_IN[1]), .Dt00(DATA_IN[0]), .S31(registrador_8_s00[31]),
    .S30(registrador_8_s00[30]), .S29(registrador_8_s00[29]), .S28(registrador_8_s00[28]),
    .S27(registrador_8_s00[27]), .S26(registrador_8_s00[26]), .S25(registrador_8_s00[25]),
    .S24(registrador_8_s00[24]), .S23(registrador_8_s00[23]), .S22(registrador_8_s00[22]),
    .S21(registrador_8_s00[21]), .S20(registrador_8_s00[20]), .S19(registrador_8_s00[19]),
    .S18(registrador_8_s00[18]), .S17(registrador_8_s00[17]), .S16(registrador_8_s00[16]),
    .S15(registrador_8_s00[15]), .S14(registrador_8_s00[14]), .S13(registrador_8_s00[13]),
    .S12(registrador_8_s00[12]), .S11(registrador_8_s00[11]), .S10(registrador_8_s00[10]),
    .S09(registrador_8_s00[9]), .S08(registrador_8_s00[8]), .S07(registrador_8_s00[7]),
    .S06(registrador_8_s00[6]), .S05(registrador_8_s00[5]), .S04(registrador_8_s00[4]),
    .S03(registrador_8_s00[3]), .S02(registrador_8_s00[2]), .S01(registrador_8_s00[1]),
    .S00(registrador_8_s00[0]));
  registrador registrador_9 (
    .write(demultiplexer_1_out14), .clear(clear), .Dt31(DATA_IN[31]), .Dt30(DATA_IN[30]), .Dt29(DATA_IN[29]),
    .Dt28(DATA_IN[28]), .Dt27(DATA_IN[27]), .Dt26(DATA_IN[26]), .Dt25(DATA_IN[25]), .Dt24(DATA_IN[24]),
    .Dt23(DATA_IN[23]), .Dt22(DATA_IN[22]), .Dt21(DATA_IN[21]), .Dt20(DATA_IN[20]), .Dt19(DATA_IN[19]),
    .Dt18(DATA_IN[18]), .Dt17(DATA_IN[17]), .Dt16(DATA_IN[16]), .Dt15(DATA_IN[15]), .Dt14(DATA_IN[14]),
    .Dt13(DATA_IN[13]), .Dt12(DATA_IN[12]), .Dt11(DATA_IN[11]), .Dt10(DATA_IN[10]), .Dt09(DATA_IN[9]),
    .Dt08(DATA_IN[8]), .Dt07(DATA_IN[7]), .Dt06(DATA_IN[6]), .Dt05(DATA_IN[5]), .Dt04(DATA_IN[4]),
    .Dt03(DATA_IN[3]), .Dt02(DATA_IN[2]), .Dt01(DATA_IN[1]), .Dt00(DATA_IN[0]), .S31(registrador_9_s00[31]),
    .S30(registrador_9_s00[30]), .S29(registrador_9_s00[29]), .S28(registrador_9_s00[28]),
    .S27(registrador_9_s00[27]), .S26(registrador_9_s00[26]), .S25(registrador_9_s00[25]),
    .S24(registrador_9_s00[24]), .S23(registrador_9_s00[23]), .S22(registrador_9_s00[22]),
    .S21(registrador_9_s00[21]), .S20(registrador_9_s00[20]), .S19(registrador_9_s00[19]),
    .S18(registrador_9_s00[18]), .S17(registrador_9_s00[17]), .S16(registrador_9_s00[16]),
    .S15(registrador_9_s00[15]), .S14(registrador_9_s00[14]), .S13(registrador_9_s00[13]),
    .S12(registrador_9_s00[12]), .S11(registrador_9_s00[11]), .S10(registrador_9_s00[10]),
    .S09(registrador_9_s00[9]), .S08(registrador_9_s00[8]), .S07(registrador_9_s00[7]),
    .S06(registrador_9_s00[6]), .S05(registrador_9_s00[5]), .S04(registrador_9_s00[4]),
    .S03(registrador_9_s00[3]), .S02(registrador_9_s00[2]), .S01(registrador_9_s00[1]),
    .S00(registrador_9_s00[0]));
  registrador registrador_10 (
    .write(demultiplexer_1_out15), .clear(clear), .Dt31(DATA_IN[31]), .Dt30(DATA_IN[30]), .Dt29(DATA_IN[29]),
    .Dt28(DATA_IN[28]), .Dt27(DATA_IN[27]), .Dt26(DATA_IN[26]), .Dt25(DATA_IN[25]), .Dt24(DATA_IN[24]),
    .Dt23(DATA_IN[23]), .Dt22(DATA_IN[22]), .Dt21(DATA_IN[21]), .Dt20(DATA_IN[20]), .Dt19(DATA_IN[19]),
    .Dt18(DATA_IN[18]), .Dt17(DATA_IN[17]), .Dt16(DATA_IN[16]), .Dt15(DATA_IN[15]), .Dt14(DATA_IN[14]),
    .Dt13(DATA_IN[13]), .Dt12(DATA_IN[12]), .Dt11(DATA_IN[11]), .Dt10(DATA_IN[10]), .Dt09(DATA_IN[9]),
    .Dt08(DATA_IN[8]), .Dt07(DATA_IN[7]), .Dt06(DATA_IN[6]), .Dt05(DATA_IN[5]), .Dt04(DATA_IN[4]),
    .Dt03(DATA_IN[3]), .Dt02(DATA_IN[2]), .Dt01(DATA_IN[1]), .Dt00(DATA_IN[0]), .S31(registrador_10_s00[31]),
    .S30(registrador_10_s00[30]), .S29(registrador_10_s00[29]), .S28(registrador_10_s00[28]),
    .S27(registrador_10_s00[27]), .S26(registrador_10_s00[26]), .S25(registrador_10_s00[25]),
    .S24(registrador_10_s00[24]), .S23(registrador_10_s00[23]), .S22(registrador_10_s00[22]),
    .S21(registrador_10_s00[21]), .S20(registrador_10_s00[20]), .S19(registrador_10_s00[19]),
    .S18(registrador_10_s00[18]), .S17(registrador_10_s00[17]), .S16(registrador_10_s00[16]),
    .S15(registrador_10_s00[15]), .S14(registrador_10_s00[14]), .S13(registrador_10_s00[13]),
    .S12(registrador_10_s00[12]), .S11(registrador_10_s00[11]), .S10(registrador_10_s00[10]),
    .S09(registrador_10_s00[9]), .S08(registrador_10_s00[8]), .S07(registrador_10_s00[7]),
    .S06(registrador_10_s00[6]), .S05(registrador_10_s00[5]), .S04(registrador_10_s00[4]),
    .S03(registrador_10_s00[3]), .S02(registrador_10_s00[2]), .S01(registrador_10_s00[1]),
    .S00(registrador_10_s00[0]));
  registrador registrador_11 (
    .write(demultiplexer_1_out16), .clear(clear), .Dt31(DATA_IN[31]), .Dt30(DATA_IN[30]), .Dt29(DATA_IN[29]),
    .Dt28(DATA_IN[28]), .Dt27(DATA_IN[27]), .Dt26(DATA_IN[26]), .Dt25(DATA_IN[25]), .Dt24(DATA_IN[24]),
    .Dt23(DATA_IN[23]), .Dt22(DATA_IN[22]), .Dt21(DATA_IN[21]), .Dt20(DATA_IN[20]), .Dt19(DATA_IN[19]),
    .Dt18(DATA_IN[18]), .Dt17(DATA_IN[17]), .Dt16(DATA_IN[16]), .Dt15(DATA_IN[15]), .Dt14(DATA_IN[14]),
    .Dt13(DATA_IN[13]), .Dt12(DATA_IN[12]), .Dt11(DATA_IN[11]), .Dt10(DATA_IN[10]), .Dt09(DATA_IN[9]),
    .Dt08(DATA_IN[8]), .Dt07(DATA_IN[7]), .Dt06(DATA_IN[6]), .Dt05(DATA_IN[5]), .Dt04(DATA_IN[4]),
    .Dt03(DATA_IN[3]), .Dt02(DATA_IN[2]), .Dt01(DATA_IN[1]), .Dt00(DATA_IN[0]), .S31(registrador_11_s00[31]),
    .S30(registrador_11_s00[30]), .S29(registrador_11_s00[29]), .S28(registrador_11_s00[28]),
    .S27(registrador_11_s00[27]), .S26(registrador_11_s00[26]), .S25(registrador_11_s00[25]),
    .S24(registrador_11_s00[24]), .S23(registrador_11_s00[23]), .S22(registrador_11_s00[22]),
    .S21(registrador_11_s00[21]), .S20(registrador_11_s00[20]), .S19(registrador_11_s00[19]),
    .S18(registrador_11_s00[18]), .S17(registrador_11_s00[17]), .S16(registrador_11_s00[16]),
    .S15(registrador_11_s00[15]), .S14(registrador_11_s00[14]), .S13(registrador_11_s00[13]),
    .S12(registrador_11_s00[12]), .S11(registrador_11_s00[11]), .S10(registrador_11_s00[10]),
    .S09(registrador_11_s00[9]), .S08(registrador_11_s00[8]), .S07(registrador_11_s00[7]),
    .S06(registrador_11_s00[6]), .S05(registrador_11_s00[5]), .S04(registrador_11_s00[4]),
    .S03(registrador_11_s00[3]), .S02(registrador_11_s00[2]), .S01(registrador_11_s00[1]),
    .S00(registrador_11_s00[0]));
  registrador registrador_12 (
    .write(demultiplexer_1_out17), .clear(clear), .Dt31(DATA_IN[31]), .Dt30(DATA_IN[30]), .Dt29(DATA_IN[29]),
    .Dt28(DATA_IN[28]), .Dt27(DATA_IN[27]), .Dt26(DATA_IN[26]), .Dt25(DATA_IN[25]), .Dt24(DATA_IN[24]),
    .Dt23(DATA_IN[23]), .Dt22(DATA_IN[22]), .Dt21(DATA_IN[21]), .Dt20(DATA_IN[20]), .Dt19(DATA_IN[19]),
    .Dt18(DATA_IN[18]), .Dt17(DATA_IN[17]), .Dt16(DATA_IN[16]), .Dt15(DATA_IN[15]), .Dt14(DATA_IN[14]),
    .Dt13(DATA_IN[13]), .Dt12(DATA_IN[12]), .Dt11(DATA_IN[11]), .Dt10(DATA_IN[10]), .Dt09(DATA_IN[9]),
    .Dt08(DATA_IN[8]), .Dt07(DATA_IN[7]), .Dt06(DATA_IN[6]), .Dt05(DATA_IN[5]), .Dt04(DATA_IN[4]),
    .Dt03(DATA_IN[3]), .Dt02(DATA_IN[2]), .Dt01(DATA_IN[1]), .Dt00(DATA_IN[0]), .S31(registrador_12_s00[31]),
    .S30(registrador_12_s00[30]), .S29(registrador_12_s00[29]), .S28(registrador_12_s00[28]),
    .S27(registrador_12_s00[27]), .S26(registrador_12_s00[26]), .S25(registrador_12_s00[25]),
    .S24(registrador_12_s00[24]), .S23(registrador_12_s00[23]), .S22(registrador_12_s00[22]),
    .S21(registrador_12_s00[21]), .S20(registrador_12_s00[20]), .S19(registrador_12_s00[19]),
    .S18(registrador_12_s00[18]), .S17(registrador_12_s00[17]), .S16(registrador_12_s00[16]),
    .S15(registrador_12_s00[15]), .S14(registrador_12_s00[14]), .S13(registrador_12_s00[13]),
    .S12(registrador_12_s00[12]), .S11(registrador_12_s00[11]), .S10(registrador_12_s00[10]),
    .S09(registrador_12_s00[9]), .S08(registrador_12_s00[8]), .S07(registrador_12_s00[7]),
    .S06(registrador_12_s00[6]), .S05(registrador_12_s00[5]), .S04(registrador_12_s00[4]),
    .S03(registrador_12_s00[3]), .S02(registrador_12_s00[2]), .S01(registrador_12_s00[1]),
    .S00(registrador_12_s00[0]));
  registrador registrador_13 (
    .write(demultiplexer_1_out18), .clear(clear), .Dt31(DATA_IN[31]), .Dt30(DATA_IN[30]), .Dt29(DATA_IN[29]),
    .Dt28(DATA_IN[28]), .Dt27(DATA_IN[27]), .Dt26(DATA_IN[26]), .Dt25(DATA_IN[25]), .Dt24(DATA_IN[24]),
    .Dt23(DATA_IN[23]), .Dt22(DATA_IN[22]), .Dt21(DATA_IN[21]), .Dt20(DATA_IN[20]), .Dt19(DATA_IN[19]),
    .Dt18(DATA_IN[18]), .Dt17(DATA_IN[17]), .Dt16(DATA_IN[16]), .Dt15(DATA_IN[15]), .Dt14(DATA_IN[14]),
    .Dt13(DATA_IN[13]), .Dt12(DATA_IN[12]), .Dt11(DATA_IN[11]), .Dt10(DATA_IN[10]), .Dt09(DATA_IN[9]),
    .Dt08(DATA_IN[8]), .Dt07(DATA_IN[7]), .Dt06(DATA_IN[6]), .Dt05(DATA_IN[5]), .Dt04(DATA_IN[4]),
    .Dt03(DATA_IN[3]), .Dt02(DATA_IN[2]), .Dt01(DATA_IN[1]), .Dt00(DATA_IN[0]), .S31(registrador_13_s00[31]),
    .S30(registrador_13_s00[30]), .S29(registrador_13_s00[29]), .S28(registrador_13_s00[28]),
    .S27(registrador_13_s00[27]), .S26(registrador_13_s00[26]), .S25(registrador_13_s00[25]),
    .S24(registrador_13_s00[24]), .S23(registrador_13_s00[23]), .S22(registrador_13_s00[22]),
    .S21(registrador_13_s00[21]), .S20(registrador_13_s00[20]), .S19(registrador_13_s00[19]),
    .S18(registrador_13_s00[18]), .S17(registrador_13_s00[17]), .S16(registrador_13_s00[16]),
    .S15(registrador_13_s00[15]), .S14(registrador_13_s00[14]), .S13(registrador_13_s00[13]),
    .S12(registrador_13_s00[12]), .S11(registrador_13_s00[11]), .S10(registrador_13_s00[10]),
    .S09(registrador_13_s00[9]), .S08(registrador_13_s00[8]), .S07(registrador_13_s00[7]),
    .S06(registrador_13_s00[6]), .S05(registrador_13_s00[5]), .S04(registrador_13_s00[4]),
    .S03(registrador_13_s00[3]), .S02(registrador_13_s00[2]), .S01(registrador_13_s00[1]),
    .S00(registrador_13_s00[0]));
  registrador registrador_14 (
    .write(demultiplexer_1_out19), .clear(clear), .Dt31(DATA_IN[31]), .Dt30(DATA_IN[30]), .Dt29(DATA_IN[29]),
    .Dt28(DATA_IN[28]), .Dt27(DATA_IN[27]), .Dt26(DATA_IN[26]), .Dt25(DATA_IN[25]), .Dt24(DATA_IN[24]),
    .Dt23(DATA_IN[23]), .Dt22(DATA_IN[22]), .Dt21(DATA_IN[21]), .Dt20(DATA_IN[20]), .Dt19(DATA_IN[19]),
    .Dt18(DATA_IN[18]), .Dt17(DATA_IN[17]), .Dt16(DATA_IN[16]), .Dt15(DATA_IN[15]), .Dt14(DATA_IN[14]),
    .Dt13(DATA_IN[13]), .Dt12(DATA_IN[12]), .Dt11(DATA_IN[11]), .Dt10(DATA_IN[10]), .Dt09(DATA_IN[9]),
    .Dt08(DATA_IN[8]), .Dt07(DATA_IN[7]), .Dt06(DATA_IN[6]), .Dt05(DATA_IN[5]), .Dt04(DATA_IN[4]),
    .Dt03(DATA_IN[3]), .Dt02(DATA_IN[2]), .Dt01(DATA_IN[1]), .Dt00(DATA_IN[0]), .S31(registrador_14_s00[31]),
    .S30(registrador_14_s00[30]), .S29(registrador_14_s00[29]), .S28(registrador_14_s00[28]),
    .S27(registrador_14_s00[27]), .S26(registrador_14_s00[26]), .S25(registrador_14_s00[25]),
    .S24(registrador_14_s00[24]), .S23(registrador_14_s00[23]), .S22(registrador_14_s00[22]),
    .S21(registrador_14_s00[21]), .S20(registrador_14_s00[20]), .S19(registrador_14_s00[19]),
    .S18(registrador_14_s00[18]), .S17(registrador_14_s00[17]), .S16(registrador_14_s00[16]),
    .S15(registrador_14_s00[15]), .S14(registrador_14_s00[14]), .S13(registrador_14_s00[13]),
    .S12(registrador_14_s00[12]), .S11(registrador_14_s00[11]), .S10(registrador_14_s00[10]),
    .S09(registrador_14_s00[9]), .S08(registrador_14_s00[8]), .S07(registrador_14_s00[7]),
    .S06(registrador_14_s00[6]), .S05(registrador_14_s00[5]), .S04(registrador_14_s00[4]),
    .S03(registrador_14_s00[3]), .S02(registrador_14_s00[2]), .S01(registrador_14_s00[1]),
    .S00(registrador_14_s00[0]));
  registrador registrador_15 (
    .write(demultiplexer_1_out20), .clear(clear), .Dt31(DATA_IN[31]), .Dt30(DATA_IN[30]), .Dt29(DATA_IN[29]),
    .Dt28(DATA_IN[28]), .Dt27(DATA_IN[27]), .Dt26(DATA_IN[26]), .Dt25(DATA_IN[25]), .Dt24(DATA_IN[24]),
    .Dt23(DATA_IN[23]), .Dt22(DATA_IN[22]), .Dt21(DATA_IN[21]), .Dt20(DATA_IN[20]), .Dt19(DATA_IN[19]),
    .Dt18(DATA_IN[18]), .Dt17(DATA_IN[17]), .Dt16(DATA_IN[16]), .Dt15(DATA_IN[15]), .Dt14(DATA_IN[14]),
    .Dt13(DATA_IN[13]), .Dt12(DATA_IN[12]), .Dt11(DATA_IN[11]), .Dt10(DATA_IN[10]), .Dt09(DATA_IN[9]),
    .Dt08(DATA_IN[8]), .Dt07(DATA_IN[7]), .Dt06(DATA_IN[6]), .Dt05(DATA_IN[5]), .Dt04(DATA_IN[4]),
    .Dt03(DATA_IN[3]), .Dt02(DATA_IN[2]), .Dt01(DATA_IN[1]), .Dt00(DATA_IN[0]), .S31(registrador_15_s00[31]),
    .S30(registrador_15_s00[30]), .S29(registrador_15_s00[29]), .S28(registrador_15_s00[28]),
    .S27(registrador_15_s00[27]), .S26(registrador_15_s00[26]), .S25(registrador_15_s00[25]),
    .S24(registrador_15_s00[24]), .S23(registrador_15_s00[23]), .S22(registrador_15_s00[22]),
    .S21(registrador_15_s00[21]), .S20(registrador_15_s00[20]), .S19(registrador_15_s00[19]),
    .S18(registrador_15_s00[18]), .S17(registrador_15_s00[17]), .S16(registrador_15_s00[16]),
    .S15(registrador_15_s00[15]), .S14(registrador_15_s00[14]), .S13(registrador_15_s00[13]),
    .S12(registrador_15_s00[12]), .S11(registrador_15_s00[11]), .S10(registrador_15_s00[10]),
    .S09(registrador_15_s00[9]), .S08(registrador_15_s00[8]), .S07(registrador_15_s00[7]),
    .S06(registrador_15_s00[6]), .S05(registrador_15_s00[5]), .S04(registrador_15_s00[4]),
    .S03(registrador_15_s00[3]), .S02(registrador_15_s00[2]), .S01(registrador_15_s00[1]),
    .S00(registrador_15_s00[0]));
  registrador registrador_16 (
    .write(demultiplexer_1_out21), .clear(clear), .Dt31(DATA_IN[31]), .Dt30(DATA_IN[30]), .Dt29(DATA_IN[29]),
    .Dt28(DATA_IN[28]), .Dt27(DATA_IN[27]), .Dt26(DATA_IN[26]), .Dt25(DATA_IN[25]), .Dt24(DATA_IN[24]),
    .Dt23(DATA_IN[23]), .Dt22(DATA_IN[22]), .Dt21(DATA_IN[21]), .Dt20(DATA_IN[20]), .Dt19(DATA_IN[19]),
    .Dt18(DATA_IN[18]), .Dt17(DATA_IN[17]), .Dt16(DATA_IN[16]), .Dt15(DATA_IN[15]), .Dt14(DATA_IN[14]),
    .Dt13(DATA_IN[13]), .Dt12(DATA_IN[12]), .Dt11(DATA_IN[11]), .Dt10(DATA_IN[10]), .Dt09(DATA_IN[9]),
    .Dt08(DATA_IN[8]), .Dt07(DATA_IN[7]), .Dt06(DATA_IN[6]), .Dt05(DATA_IN[5]), .Dt04(DATA_IN[4]),
    .Dt03(DATA_IN[3]), .Dt02(DATA_IN[2]), .Dt01(DATA_IN[1]), .Dt00(DATA_IN[0]), .S31(registrador_16_s00[31]),
    .S30(registrador_16_s00[30]), .S29(registrador_16_s00[29]), .S28(registrador_16_s00[28]),
    .S27(registrador_16_s00[27]), .S26(registrador_16_s00[26]), .S25(registrador_16_s00[25]),
    .S24(registrador_16_s00[24]), .S23(registrador_16_s00[23]), .S22(registrador_16_s00[22]),
    .S21(registrador_16_s00[21]), .S20(registrador_16_s00[20]), .S19(registrador_16_s00[19]),
    .S18(registrador_16_s00[18]), .S17(registrador_16_s00[17]), .S16(registrador_16_s00[16]),
    .S15(registrador_16_s00[15]), .S14(registrador_16_s00[14]), .S13(registrador_16_s00[13]),
    .S12(registrador_16_s00[12]), .S11(registrador_16_s00[11]), .S10(registrador_16_s00[10]),
    .S09(registrador_16_s00[9]), .S08(registrador_16_s00[8]), .S07(registrador_16_s00[7]),
    .S06(registrador_16_s00[6]), .S05(registrador_16_s00[5]), .S04(registrador_16_s00[4]),
    .S03(registrador_16_s00[3]), .S02(registrador_16_s00[2]), .S01(registrador_16_s00[1]),
    .S00(registrador_16_s00[0]));
  registrador registrador_17 (
    .write(demultiplexer_1_out22), .clear(clear), .Dt31(DATA_IN[31]), .Dt30(DATA_IN[30]), .Dt29(DATA_IN[29]),
    .Dt28(DATA_IN[28]), .Dt27(DATA_IN[27]), .Dt26(DATA_IN[26]), .Dt25(DATA_IN[25]), .Dt24(DATA_IN[24]),
    .Dt23(DATA_IN[23]), .Dt22(DATA_IN[22]), .Dt21(DATA_IN[21]), .Dt20(DATA_IN[20]), .Dt19(DATA_IN[19]),
    .Dt18(DATA_IN[18]), .Dt17(DATA_IN[17]), .Dt16(DATA_IN[16]), .Dt15(DATA_IN[15]), .Dt14(DATA_IN[14]),
    .Dt13(DATA_IN[13]), .Dt12(DATA_IN[12]), .Dt11(DATA_IN[11]), .Dt10(DATA_IN[10]), .Dt09(DATA_IN[9]),
    .Dt08(DATA_IN[8]), .Dt07(DATA_IN[7]), .Dt06(DATA_IN[6]), .Dt05(DATA_IN[5]), .Dt04(DATA_IN[4]),
    .Dt03(DATA_IN[3]), .Dt02(DATA_IN[2]), .Dt01(DATA_IN[1]), .Dt00(DATA_IN[0]), .S31(registrador_17_s00[31]),
    .S30(registrador_17_s00[30]), .S29(registrador_17_s00[29]), .S28(registrador_17_s00[28]),
    .S27(registrador_17_s00[27]), .S26(registrador_17_s00[26]), .S25(registrador_17_s00[25]),
    .S24(registrador_17_s00[24]), .S23(registrador_17_s00[23]), .S22(registrador_17_s00[22]),
    .S21(registrador_17_s00[21]), .S20(registrador_17_s00[20]), .S19(registrador_17_s00[19]),
    .S18(registrador_17_s00[18]), .S17(registrador_17_s00[17]), .S16(registrador_17_s00[16]),
    .S15(registrador_17_s00[15]), .S14(registrador_17_s00[14]), .S13(registrador_17_s00[13]),
    .S12(registrador_17_s00[12]), .S11(registrador_17_s00[11]), .S10(registrador_17_s00[10]),
    .S09(registrador_17_s00[9]), .S08(registrador_17_s00[8]), .S07(registrador_17_s00[7]),
    .S06(registrador_17_s00[6]), .S05(registrador_17_s00[5]), .S04(registrador_17_s00[4]),
    .S03(registrador_17_s00[3]), .S02(registrador_17_s00[2]), .S01(registrador_17_s00[1]),
    .S00(registrador_17_s00[0]));
  registrador registrador_18 (
    .write(demultiplexer_1_out23), .clear(clear), .Dt31(DATA_IN[31]), .Dt30(DATA_IN[30]), .Dt29(DATA_IN[29]),
    .Dt28(DATA_IN[28]), .Dt27(DATA_IN[27]), .Dt26(DATA_IN[26]), .Dt25(DATA_IN[25]), .Dt24(DATA_IN[24]),
    .Dt23(DATA_IN[23]), .Dt22(DATA_IN[22]), .Dt21(DATA_IN[21]), .Dt20(DATA_IN[20]), .Dt19(DATA_IN[19]),
    .Dt18(DATA_IN[18]), .Dt17(DATA_IN[17]), .Dt16(DATA_IN[16]), .Dt15(DATA_IN[15]), .Dt14(DATA_IN[14]),
    .Dt13(DATA_IN[13]), .Dt12(DATA_IN[12]), .Dt11(DATA_IN[11]), .Dt10(DATA_IN[10]), .Dt09(DATA_IN[9]),
    .Dt08(DATA_IN[8]), .Dt07(DATA_IN[7]), .Dt06(DATA_IN[6]), .Dt05(DATA_IN[5]), .Dt04(DATA_IN[4]),
    .Dt03(DATA_IN[3]), .Dt02(DATA_IN[2]), .Dt01(DATA_IN[1]), .Dt00(DATA_IN[0]), .S31(registrador_18_s00[31]),
    .S30(registrador_18_s00[30]), .S29(registrador_18_s00[29]), .S28(registrador_18_s00[28]),
    .S27(registrador_18_s00[27]), .S26(registrador_18_s00[26]), .S25(registrador_18_s00[25]),
    .S24(registrador_18_s00[24]), .S23(registrador_18_s00[23]), .S22(registrador_18_s00[22]),
    .S21(registrador_18_s00[21]), .S20(registrador_18_s00[20]), .S19(registrador_18_s00[19]),
    .S18(registrador_18_s00[18]), .S17(registrador_18_s00[17]), .S16(registrador_18_s00[16]),
    .S15(registrador_18_s00[15]), .S14(registrador_18_s00[14]), .S13(registrador_18_s00[13]),
    .S12(registrador_18_s00[12]), .S11(registrador_18_s00[11]), .S10(registrador_18_s00[10]),
    .S09(registrador_18_s00[9]), .S08(registrador_18_s00[8]), .S07(registrador_18_s00[7]),
    .S06(registrador_18_s00[6]), .S05(registrador_18_s00[5]), .S04(registrador_18_s00[4]),
    .S03(registrador_18_s00[3]), .S02(registrador_18_s00[2]), .S01(registrador_18_s00[1]),
    .S00(registrador_18_s00[0]));
  registrador registrador_19 (
    .write(demultiplexer_1_out24), .clear(clear), .Dt31(DATA_IN[31]), .Dt30(DATA_IN[30]), .Dt29(DATA_IN[29]),
    .Dt28(DATA_IN[28]), .Dt27(DATA_IN[27]), .Dt26(DATA_IN[26]), .Dt25(DATA_IN[25]), .Dt24(DATA_IN[24]),
    .Dt23(DATA_IN[23]), .Dt22(DATA_IN[22]), .Dt21(DATA_IN[21]), .Dt20(DATA_IN[20]), .Dt19(DATA_IN[19]),
    .Dt18(DATA_IN[18]), .Dt17(DATA_IN[17]), .Dt16(DATA_IN[16]), .Dt15(DATA_IN[15]), .Dt14(DATA_IN[14]),
    .Dt13(DATA_IN[13]), .Dt12(DATA_IN[12]), .Dt11(DATA_IN[11]), .Dt10(DATA_IN[10]), .Dt09(DATA_IN[9]),
    .Dt08(DATA_IN[8]), .Dt07(DATA_IN[7]), .Dt06(DATA_IN[6]), .Dt05(DATA_IN[5]), .Dt04(DATA_IN[4]),
    .Dt03(DATA_IN[3]), .Dt02(DATA_IN[2]), .Dt01(DATA_IN[1]), .Dt00(DATA_IN[0]), .S31(registrador_19_s00[31]),
    .S30(registrador_19_s00[30]), .S29(registrador_19_s00[29]), .S28(registrador_19_s00[28]),
    .S27(registrador_19_s00[27]), .S26(registrador_19_s00[26]), .S25(registrador_19_s00[25]),
    .S24(registrador_19_s00[24]), .S23(registrador_19_s00[23]), .S22(registrador_19_s00[22]),
    .S21(registrador_19_s00[21]), .S20(registrador_19_s00[20]), .S19(registrador_19_s00[19]),
    .S18(registrador_19_s00[18]), .S17(registrador_19_s00[17]), .S16(registrador_19_s00[16]),
    .S15(registrador_19_s00[15]), .S14(registrador_19_s00[14]), .S13(registrador_19_s00[13]),
    .S12(registrador_19_s00[12]), .S11(registrador_19_s00[11]), .S10(registrador_19_s00[10]),
    .S09(registrador_19_s00[9]), .S08(registrador_19_s00[8]), .S07(registrador_19_s00[7]),
    .S06(registrador_19_s00[6]), .S05(registrador_19_s00[5]), .S04(registrador_19_s00[4]),
    .S03(registrador_19_s00[3]), .S02(registrador_19_s00[2]), .S01(registrador_19_s00[1]),
    .S00(registrador_19_s00[0]));
  registrador registrador_20 (
    .write(demultiplexer_1_out25), .clear(clear), .Dt31(DATA_IN[31]), .Dt30(DATA_IN[30]), .Dt29(DATA_IN[29]),
    .Dt28(DATA_IN[28]), .Dt27(DATA_IN[27]), .Dt26(DATA_IN[26]), .Dt25(DATA_IN[25]), .Dt24(DATA_IN[24]),
    .Dt23(DATA_IN[23]), .Dt22(DATA_IN[22]), .Dt21(DATA_IN[21]), .Dt20(DATA_IN[20]), .Dt19(DATA_IN[19]),
    .Dt18(DATA_IN[18]), .Dt17(DATA_IN[17]), .Dt16(DATA_IN[16]), .Dt15(DATA_IN[15]), .Dt14(DATA_IN[14]),
    .Dt13(DATA_IN[13]), .Dt12(DATA_IN[12]), .Dt11(DATA_IN[11]), .Dt10(DATA_IN[10]), .Dt09(DATA_IN[9]),
    .Dt08(DATA_IN[8]), .Dt07(DATA_IN[7]), .Dt06(DATA_IN[6]), .Dt05(DATA_IN[5]), .Dt04(DATA_IN[4]),
    .Dt03(DATA_IN[3]), .Dt02(DATA_IN[2]), .Dt01(DATA_IN[1]), .Dt00(DATA_IN[0]), .S31(registrador_20_s00[31]),
    .S30(registrador_20_s00[30]), .S29(registrador_20_s00[29]), .S28(registrador_20_s00[28]),
    .S27(registrador_20_s00[27]), .S26(registrador_20_s00[26]), .S25(registrador_20_s00[25]),
    .S24(registrador_20_s00[24]), .S23(registrador_20_s00[23]), .S22(registrador_20_s00[22]),
    .S21(registrador_20_s00[21]), .S20(registrador_20_s00[20]), .S19(registrador_20_s00[19]),
    .S18(registrador_20_s00[18]), .S17(registrador_20_s00[17]), .S16(registrador_20_s00[16]),
    .S15(registrador_20_s00[15]), .S14(registrador_20_s00[14]), .S13(registrador_20_s00[13]),
    .S12(registrador_20_s00[12]), .S11(registrador_20_s00[11]), .S10(registrador_20_s00[10]),
    .S09(registrador_20_s00[9]), .S08(registrador_20_s00[8]), .S07(registrador_20_s00[7]),
    .S06(registrador_20_s00[6]), .S05(registrador_20_s00[5]), .S04(registrador_20_s00[4]),
    .S03(registrador_20_s00[3]), .S02(registrador_20_s00[2]), .S01(registrador_20_s00[1]),
    .S00(registrador_20_s00[0]));
  registrador registrador_21 (
    .write(demultiplexer_1_out26), .clear(clear), .Dt31(DATA_IN[31]), .Dt30(DATA_IN[30]), .Dt29(DATA_IN[29]),
    .Dt28(DATA_IN[28]), .Dt27(DATA_IN[27]), .Dt26(DATA_IN[26]), .Dt25(DATA_IN[25]), .Dt24(DATA_IN[24]),
    .Dt23(DATA_IN[23]), .Dt22(DATA_IN[22]), .Dt21(DATA_IN[21]), .Dt20(DATA_IN[20]), .Dt19(DATA_IN[19]),
    .Dt18(DATA_IN[18]), .Dt17(DATA_IN[17]), .Dt16(DATA_IN[16]), .Dt15(DATA_IN[15]), .Dt14(DATA_IN[14]),
    .Dt13(DATA_IN[13]), .Dt12(DATA_IN[12]), .Dt11(DATA_IN[11]), .Dt10(DATA_IN[10]), .Dt09(DATA_IN[9]),
    .Dt08(DATA_IN[8]), .Dt07(DATA_IN[7]), .Dt06(DATA_IN[6]), .Dt05(DATA_IN[5]), .Dt04(DATA_IN[4]),
    .Dt03(DATA_IN[3]), .Dt02(DATA_IN[2]), .Dt01(DATA_IN[1]), .Dt00(DATA_IN[0]), .S31(registrador_21_s00[31]),
    .S30(registrador_21_s00[30]), .S29(registrador_21_s00[29]), .S28(registrador_21_s00[28]),
    .S27(registrador_21_s00[27]), .S26(registrador_21_s00[26]), .S25(registrador_21_s00[25]),
    .S24(registrador_21_s00[24]), .S23(registrador_21_s00[23]), .S22(registrador_21_s00[22]),
    .S21(registrador_21_s00[21]), .S20(registrador_21_s00[20]), .S19(registrador_21_s00[19]),
    .S18(registrador_21_s00[18]), .S17(registrador_21_s00[17]), .S16(registrador_21_s00[16]),
    .S15(registrador_21_s00[15]), .S14(registrador_21_s00[14]), .S13(registrador_21_s00[13]),
    .S12(registrador_21_s00[12]), .S11(registrador_21_s00[11]), .S10(registrador_21_s00[10]),
    .S09(registrador_21_s00[9]), .S08(registrador_21_s00[8]), .S07(registrador_21_s00[7]),
    .S06(registrador_21_s00[6]), .S05(registrador_21_s00[5]), .S04(registrador_21_s00[4]),
    .S03(registrador_21_s00[3]), .S02(registrador_21_s00[2]), .S01(registrador_21_s00[1]),
    .S00(registrador_21_s00[0]));
  registrador registrador_22 (
    .write(demultiplexer_1_out27), .clear(clear), .Dt31(DATA_IN[31]), .Dt30(DATA_IN[30]), .Dt29(DATA_IN[29]),
    .Dt28(DATA_IN[28]), .Dt27(DATA_IN[27]), .Dt26(DATA_IN[26]), .Dt25(DATA_IN[25]), .Dt24(DATA_IN[24]),
    .Dt23(DATA_IN[23]), .Dt22(DATA_IN[22]), .Dt21(DATA_IN[21]), .Dt20(DATA_IN[20]), .Dt19(DATA_IN[19]),
    .Dt18(DATA_IN[18]), .Dt17(DATA_IN[17]), .Dt16(DATA_IN[16]), .Dt15(DATA_IN[15]), .Dt14(DATA_IN[14]),
    .Dt13(DATA_IN[13]), .Dt12(DATA_IN[12]), .Dt11(DATA_IN[11]), .Dt10(DATA_IN[10]), .Dt09(DATA_IN[9]),
    .Dt08(DATA_IN[8]), .Dt07(DATA_IN[7]), .Dt06(DATA_IN[6]), .Dt05(DATA_IN[5]), .Dt04(DATA_IN[4]),
    .Dt03(DATA_IN[3]), .Dt02(DATA_IN[2]), .Dt01(DATA_IN[1]), .Dt00(DATA_IN[0]), .S31(registrador_22_s00[31]),
    .S30(registrador_22_s00[30]), .S29(registrador_22_s00[29]), .S28(registrador_22_s00[28]),
    .S27(registrador_22_s00[27]), .S26(registrador_22_s00[26]), .S25(registrador_22_s00[25]),
    .S24(registrador_22_s00[24]), .S23(registrador_22_s00[23]), .S22(registrador_22_s00[22]),
    .S21(registrador_22_s00[21]), .S20(registrador_22_s00[20]), .S19(registrador_22_s00[19]),
    .S18(registrador_22_s00[18]), .S17(registrador_22_s00[17]), .S16(registrador_22_s00[16]),
    .S15(registrador_22_s00[15]), .S14(registrador_22_s00[14]), .S13(registrador_22_s00[13]),
    .S12(registrador_22_s00[12]), .S11(registrador_22_s00[11]), .S10(registrador_22_s00[10]),
    .S09(registrador_22_s00[9]), .S08(registrador_22_s00[8]), .S07(registrador_22_s00[7]),
    .S06(registrador_22_s00[6]), .S05(registrador_22_s00[5]), .S04(registrador_22_s00[4]),
    .S03(registrador_22_s00[3]), .S02(registrador_22_s00[2]), .S01(registrador_22_s00[1]),
    .S00(registrador_22_s00[0]));
  registrador registrador_23 (
    .write(demultiplexer_1_out28), .clear(clear), .Dt31(DATA_IN[31]), .Dt30(DATA_IN[30]), .Dt29(DATA_IN[29]),
    .Dt28(DATA_IN[28]), .Dt27(DATA_IN[27]), .Dt26(DATA_IN[26]), .Dt25(DATA_IN[25]), .Dt24(DATA_IN[24]),
    .Dt23(DATA_IN[23]), .Dt22(DATA_IN[22]), .Dt21(DATA_IN[21]), .Dt20(DATA_IN[20]), .Dt19(DATA_IN[19]),
    .Dt18(DATA_IN[18]), .Dt17(DATA_IN[17]), .Dt16(DATA_IN[16]), .Dt15(DATA_IN[15]), .Dt14(DATA_IN[14]),
    .Dt13(DATA_IN[13]), .Dt12(DATA_IN[12]), .Dt11(DATA_IN[11]), .Dt10(DATA_IN[10]), .Dt09(DATA_IN[9]),
    .Dt08(DATA_IN[8]), .Dt07(DATA_IN[7]), .Dt06(DATA_IN[6]), .Dt05(DATA_IN[5]), .Dt04(DATA_IN[4]),
    .Dt03(DATA_IN[3]), .Dt02(DATA_IN[2]), .Dt01(DATA_IN[1]), .Dt00(DATA_IN[0]), .S31(registrador_23_s00[31]),
    .S30(registrador_23_s00[30]), .S29(registrador_23_s00[29]), .S28(registrador_23_s00[28]),
    .S27(registrador_23_s00[27]), .S26(registrador_23_s00[26]), .S25(registrador_23_s00[25]),
    .S24(registrador_23_s00[24]), .S23(registrador_23_s00[23]), .S22(registrador_23_s00[22]),
    .S21(registrador_23_s00[21]), .S20(registrador_23_s00[20]), .S19(registrador_23_s00[19]),
    .S18(registrador_23_s00[18]), .S17(registrador_23_s00[17]), .S16(registrador_23_s00[16]),
    .S15(registrador_23_s00[15]), .S14(registrador_23_s00[14]), .S13(registrador_23_s00[13]),
    .S12(registrador_23_s00[12]), .S11(registrador_23_s00[11]), .S10(registrador_23_s00[10]),
    .S09(registrador_23_s00[9]), .S08(registrador_23_s00[8]), .S07(registrador_23_s00[7]),
    .S06(registrador_23_s00[6]), .S05(registrador_23_s00[5]), .S04(registrador_23_s00[4]),
    .S03(registrador_23_s00[3]), .S02(registrador_23_s00[2]), .S01(registrador_23_s00[1]),
    .S00(registrador_23_s00[0]));
  registrador registrador_24 (
    .write(demultiplexer_1_out29), .clear(clear), .Dt31(DATA_IN[31]), .Dt30(DATA_IN[30]), .Dt29(DATA_IN[29]),
    .Dt28(DATA_IN[28]), .Dt27(DATA_IN[27]), .Dt26(DATA_IN[26]), .Dt25(DATA_IN[25]), .Dt24(DATA_IN[24]),
    .Dt23(DATA_IN[23]), .Dt22(DATA_IN[22]), .Dt21(DATA_IN[21]), .Dt20(DATA_IN[20]), .Dt19(DATA_IN[19]),
    .Dt18(DATA_IN[18]), .Dt17(DATA_IN[17]), .Dt16(DATA_IN[16]), .Dt15(DATA_IN[15]), .Dt14(DATA_IN[14]),
    .Dt13(DATA_IN[13]), .Dt12(DATA_IN[12]), .Dt11(DATA_IN[11]), .Dt10(DATA_IN[10]), .Dt09(DATA_IN[9]),
    .Dt08(DATA_IN[8]), .Dt07(DATA_IN[7]), .Dt06(DATA_IN[6]), .Dt05(DATA_IN[5]), .Dt04(DATA_IN[4]),
    .Dt03(DATA_IN[3]), .Dt02(DATA_IN[2]), .Dt01(DATA_IN[1]), .Dt00(DATA_IN[0]), .S31(registrador_24_s00[31]),
    .S30(registrador_24_s00[30]), .S29(registrador_24_s00[29]), .S28(registrador_24_s00[28]),
    .S27(registrador_24_s00[27]), .S26(registrador_24_s00[26]), .S25(registrador_24_s00[25]),
    .S24(registrador_24_s00[24]), .S23(registrador_24_s00[23]), .S22(registrador_24_s00[22]),
    .S21(registrador_24_s00[21]), .S20(registrador_24_s00[20]), .S19(registrador_24_s00[19]),
    .S18(registrador_24_s00[18]), .S17(registrador_24_s00[17]), .S16(registrador_24_s00[16]),
    .S15(registrador_24_s00[15]), .S14(registrador_24_s00[14]), .S13(registrador_24_s00[13]),
    .S12(registrador_24_s00[12]), .S11(registrador_24_s00[11]), .S10(registrador_24_s00[10]),
    .S09(registrador_24_s00[9]), .S08(registrador_24_s00[8]), .S07(registrador_24_s00[7]),
    .S06(registrador_24_s00[6]), .S05(registrador_24_s00[5]), .S04(registrador_24_s00[4]),
    .S03(registrador_24_s00[3]), .S02(registrador_24_s00[2]), .S01(registrador_24_s00[1]),
    .S00(registrador_24_s00[0]));
  registrador registrador_25 (
    .write(demultiplexer_1_out30), .clear(clear), .Dt31(DATA_IN[31]), .Dt30(DATA_IN[30]), .Dt29(DATA_IN[29]),
    .Dt28(DATA_IN[28]), .Dt27(DATA_IN[27]), .Dt26(DATA_IN[26]), .Dt25(DATA_IN[25]), .Dt24(DATA_IN[24]),
    .Dt23(DATA_IN[23]), .Dt22(DATA_IN[22]), .Dt21(DATA_IN[21]), .Dt20(DATA_IN[20]), .Dt19(DATA_IN[19]),
    .Dt18(DATA_IN[18]), .Dt17(DATA_IN[17]), .Dt16(DATA_IN[16]), .Dt15(DATA_IN[15]), .Dt14(DATA_IN[14]),
    .Dt13(DATA_IN[13]), .Dt12(DATA_IN[12]), .Dt11(DATA_IN[11]), .Dt10(DATA_IN[10]), .Dt09(DATA_IN[9]),
    .Dt08(DATA_IN[8]), .Dt07(DATA_IN[7]), .Dt06(DATA_IN[6]), .Dt05(DATA_IN[5]), .Dt04(DATA_IN[4]),
    .Dt03(DATA_IN[3]), .Dt02(DATA_IN[2]), .Dt01(DATA_IN[1]), .Dt00(DATA_IN[0]), .S31(registrador_25_s00[31]),
    .S30(registrador_25_s00[30]), .S29(registrador_25_s00[29]), .S28(registrador_25_s00[28]),
    .S27(registrador_25_s00[27]), .S26(registrador_25_s00[26]), .S25(registrador_25_s00[25]),
    .S24(registrador_25_s00[24]), .S23(registrador_25_s00[23]), .S22(registrador_25_s00[22]),
    .S21(registrador_25_s00[21]), .S20(registrador_25_s00[20]), .S19(registrador_25_s00[19]),
    .S18(registrador_25_s00[18]), .S17(registrador_25_s00[17]), .S16(registrador_25_s00[16]),
    .S15(registrador_25_s00[15]), .S14(registrador_25_s00[14]), .S13(registrador_25_s00[13]),
    .S12(registrador_25_s00[12]), .S11(registrador_25_s00[11]), .S10(registrador_25_s00[10]),
    .S09(registrador_25_s00[9]), .S08(registrador_25_s00[8]), .S07(registrador_25_s00[7]),
    .S06(registrador_25_s00[6]), .S05(registrador_25_s00[5]), .S04(registrador_25_s00[4]),
    .S03(registrador_25_s00[3]), .S02(registrador_25_s00[2]), .S01(registrador_25_s00[1]),
    .S00(registrador_25_s00[0]));
  registrador registrador_26 (
    .write(demultiplexer_1_out31), .clear(clear), .Dt31(DATA_IN[31]), .Dt30(DATA_IN[30]), .Dt29(DATA_IN[29]),
    .Dt28(DATA_IN[28]), .Dt27(DATA_IN[27]), .Dt26(DATA_IN[26]), .Dt25(DATA_IN[25]), .Dt24(DATA_IN[24]),
    .Dt23(DATA_IN[23]), .Dt22(DATA_IN[22]), .Dt21(DATA_IN[21]), .Dt20(DATA_IN[20]), .Dt19(DATA_IN[19]),
    .Dt18(DATA_IN[18]), .Dt17(DATA_IN[17]), .Dt16(DATA_IN[16]), .Dt15(DATA_IN[15]), .Dt14(DATA_IN[14]),
    .Dt13(DATA_IN[13]), .Dt12(DATA_IN[12]), .Dt11(DATA_IN[11]), .Dt10(DATA_IN[10]), .Dt09(DATA_IN[9]),
    .Dt08(DATA_IN[8]), .Dt07(DATA_IN[7]), .Dt06(DATA_IN[6]), .Dt05(DATA_IN[5]), .Dt04(DATA_IN[4]),
    .Dt03(DATA_IN[3]), .Dt02(DATA_IN[2]), .Dt01(DATA_IN[1]), .Dt00(DATA_IN[0]), .S31(registrador_26_s00[31]),
    .S30(registrador_26_s00[30]), .S29(registrador_26_s00[29]), .S28(registrador_26_s00[28]),
    .S27(registrador_26_s00[27]), .S26(registrador_26_s00[26]), .S25(registrador_26_s00[25]),
    .S24(registrador_26_s00[24]), .S23(registrador_26_s00[23]), .S22(registrador_26_s00[22]),
    .S21(registrador_26_s00[21]), .S20(registrador_26_s00[20]), .S19(registrador_26_s00[19]),
    .S18(registrador_26_s00[18]), .S17(registrador_26_s00[17]), .S16(registrador_26_s00[16]),
    .S15(registrador_26_s00[15]), .S14(registrador_26_s00[14]), .S13(registrador_26_s00[13]),
    .S12(registrador_26_s00[12]), .S11(registrador_26_s00[11]), .S10(registrador_26_s00[10]),
    .S09(registrador_26_s00[9]), .S08(registrador_26_s00[8]), .S07(registrador_26_s00[7]),
    .S06(registrador_26_s00[6]), .S05(registrador_26_s00[5]), .S04(registrador_26_s00[4]),
    .S03(registrador_26_s00[3]), .S02(registrador_26_s00[2]), .S01(registrador_26_s00[1]),
    .S00(registrador_26_s00[0]));
  Multiplexer #(.select(5), .width(32), .enable("false")) multiplexer_1 (
    .in0(_00000_s00), .in1(_00001_s00), .in2(_00010_s00), .in3(_00011_s00), .in4(_00100_s00),
    .in5(_00101_s00), .in6(registrador_1_s00), .in7(registrador_2_s00), .in8(registrador_3_s00),
    .in9(registrador_4_s00), .in10(registrador_5_s00), .in11(registrador_6_s00), .in12(registrador_7_s00),
    .in13(registrador_8_s00), .in14(registrador_9_s00), .in15(registrador_10_s00), .in16(registrador_11_s00),
    .in17(registrador_12_s00), .in18(registrador_13_s00), .in19(registrador_14_s00),
    .in20(registrador_15_s00), .in21(registrador_16_s00), .in22(registrador_17_s00),
    .in23(registrador_18_s00), .in24(registrador_19_s00), .in25(registrador_20_s00),
    .in26(registrador_21_s00), .in27(registrador_22_s00), .in28(registrador_23_s00),
    .in29(registrador_24_s00), .in30(registrador_25_s00), .in31(registrador_26_s00), .out(DATAreg_A),
    .sel(registrador_A));
  Multiplexer #(.select(5), .width(32), .enable("false")) multiplexer_2 (
    .in0(_00000_s00), .in1(_00001_s00), .in2(_00010_s00), .in3(_00011_s00), .in4(_00100_s00),
    .in5(_00101_s00), .in6(registrador_1_s00), .in7(registrador_2_s00), .in8(registrador_3_s00),
    .in9(registrador_4_s00), .in10(registrador_5_s00), .in11(registrador_6_s00), .in12(registrador_7_s00),
    .in13(registrador_8_s00), .in14(registrador_9_s00), .in15(registrador_10_s00), .in16(registrador_11_s00),
    .in17(registrador_12_s00), .in18(registrador_13_s00), .in19(registrador_14_s00),
    .in20(registrador_15_s00), .in21(registrador_16_s00), .in22(registrador_17_s00),
    .in23(registrador_18_s00), .in24(registrador_19_s00), .in25(registrador_20_s00),
    .in26(registrador_21_s00), .in27(registrador_22_s00), .in28(registrador_23_s00),
    .in29(registrador_24_s00), .in30(registrador_25_s00), .in31(registrador_26_s00), .out(DATAreg_B),
    .sel(registrador_B));
endmodule
module PC_MEM (
  input  [9:0] estado_do_salto,
  input  saltar,
  input  RESET,
  input  PC_CLK,
  output [31:0] MEMout
);

  wire [9:0] adder_1_out, multiplexer_1_out, PC_q;

  Multiplexer #(.width(10), .enable("false")) multiplexer_1 (
    .in0(10'h1), .in1(estado_do_salto), .out(multiplexer_1_out), .sel(saltar));
  Register #(.width(10)) PC (.D(adder_1_out), .Q(PC_q), .clk(PC_CLK), .clr(RESET));  // open: en
  Adder #(.width(10)) adder_1 (.a(multiplexer_1_out), .b(PC_q), .out(adder_1_out));  // open: cin, cout
  RAM #(.addrWidth(10), .dataWidth(32)) ram_1 (.addr(PC_q), .data(MEMout));  // open: sel, clk, ld, clr
endmodule

module comparador (
  input  [31:0] in_1,
  input  [31:0] in_2,
  output out_3
);

  wire xnor_1_out, xnor_2_out, xnor_3_out, xnor_4_out, xnor_5_out, xnor_6_out, xnor_7_out, xnor_8_out,
       xnor_9_out, xnor_10_out, xnor_11_out, xnor_12_out, xnor_13_out, xnor_14_out, xnor_15_out, xnor_16_out,
       xnor_17_out, xnor_18_out, xnor_19_out, xnor_20_out, xnor_21_out, xnor_22_out, xnor_23_out,
       xnor_24_out, xnor_25_out, xnor_26_out, xnor_27_out, xnor_28_out, xnor_29_out, xnor_30_out,
       xnor_31_out, xnor_32_out;

  xnor xnor_1 (xnor_1_out, in_1[0], in_2[0]);
  xnor xnor_2 (xnor_2_out, in_1[1], in_2[1]);
  xnor xnor_3 (xnor_3_out, in_1[2], in_2[2]);
  xnor xnor_4 (xnor_4_out, in_1[3], in_2[3]);
  xnor xnor_5 (xnor_5_out, in_1[4], in_2[4]);
  xnor xnor_6 (xnor_6_out, in_1[5], in_2[5]);
  xnor xnor_7 (xnor_7_out, in_1[6], in_2[6]);
  xnor xnor_8 (xnor_8_out, in_1[7], in_2[7]);
  xnor xnor_9 (xnor_9_out, in_1[8], in_2[8]);
  xnor xnor_10 (xnor_10_out, in_1[9], in_2[9]);
  xnor xnor_11 (xnor_11_out, in_1[10], in_2[10]);
  xnor xnor_12 (xnor_12_out, in_1[11], in_2[11]);
  xnor xnor_13 (xnor_13_out, in_1[12], in_2[12]);
  xnor xnor_14 (xnor_14_out, in_1[13], in_2[13]);
  xnor xnor_15 (xnor_15_out, in_1[14], in_2[14]);
  xnor xnor_16 (xnor_16_out, in_1[15], in_2[15]);
  xnor xnor_17 (xnor_17_out, in_1[16], in_2[16]);
  xnor xnor_18 (xnor_18_out, in_1[17], in_2[17]);
  xnor xnor_19 (xnor_19_out, in_1[18], in_2[18]);
  xnor xnor_20 (xnor_20_out, in_1[19], in_2[19]);
  xnor xnor_21 (xnor_21_out, in_1[20], in_2[20]);
  xnor xnor_22 (xnor_22_out, in_1[21], in_2[21]);
  xnor xnor_23 (xnor_23_out, in_1[22], in_2[22]);
  xnor xnor_24 (xnor_24_out, in_1[23], in_2[23]);
  xnor xnor_25 (xnor_25_out, in_1[24], in_2[24]);
  xnor xnor_26 (xnor_26_out, in_1[25], in_2[25]);
  xnor xnor_27 (xnor_27_out, in_1[26], in_2[26]);
  xnor xnor_28 (xnor_28_out, in_1[27], in_2[27]);
  xnor xnor_29 (xnor_29_out, in_1[28], in_2[28]);
  xnor xnor_30 (xnor_30_out, in_1[29], in_2[29]);
  xnor xnor_31 (xnor_31_out, in_1[30], in_2[30]);
  xnor xnor_32 (xnor_32_out, in_1[31], in_2[31]);
  and and_1 (out_3, xnor_1_out, xnor_2_out, xnor_3_out, xnor_4_out, xnor_5_out, xnor_6_out, xnor_7_out, xnor_8_out, xnor_9_out, xnor_10_out, xnor_11_out, xnor_12_out, xnor_13_out, xnor_14_out, xnor_15_out, xnor_16_out, xnor_17_out, xnor_18_out, xnor_19_out, xnor_20_out, xnor_21_out, xnor_22_out, xnor_23_out, xnor_24_out, xnor_25_out, xnor_26_out, xnor_27_out, xnor_28_out, xnor_29_out, xnor_30_out, xnor_31_out, xnor_32_out);
endmodule

module teste_memmoria (
  input  in_1,
  input  in_2,
  input  in_3,
  input  [7:0] in_4
);

  wire clock_1_out;
  wire [3:0] adder_1_out, multiplexer_1_out, multiplexer_1_out_2, register_1_q;

  _7_Segment_Display u_7_segment_display_1 (
    .g(multiplexer_1_out[3]), .f(multiplexer_1_out[2]), .a(multiplexer_1_out[1]), .b(multiplexer_1_out[0]),
    .e(multiplexer_1_out_2[3]), .d(multiplexer_1_out_2[2]), .c(multiplexer_1_out_2[1]),
    .dp(multiplexer_1_out_2[0]));
  Adder #(.width(4)) adder_1 (.a(4'b0001), .b(register_1_q), .out(adder_1_out));  // open: cin, cout
  Register #(.width(4)) register_1 (.D(adder_1_out), .Q(register_1_q), .clk(in_1), .clr(in_2));  // open: en
  Clock clock_1 (.out(clock_1_out));
  Multiplexer #(.width(8), .enable("false")) multiplexer_1 (
    .in0(in_4), .in1({multiplexer_1_out, multiplexer_1_out_2}),
    .out({multiplexer_1_out, multiplexer_1_out_2}), .sel(in_3));
  RAM #(.addrWidth(4)) ram_1 (
    .addr(register_1_q), .data({multiplexer_1_out, multiplexer_1_out_2}), .clk(clock_1_out), .ld(in_3));  // open: sel, clr
endmodule
